// Logisim project PC TESTS.circ as structural Verilog: 1 circuit, main circuit main
module main (
  input  in_1
);

  wire A_____PROVE, A_____RAM, ADD_A___B, and_1_out, B_____RAM, buffer_2_out, buffer_4_out, buffer_6_out,
       buffer_9_out, buffer_10_out, buffer_11_out, buffer_35_out, buffer_36_out, buffer_37_out,
       buffer_38_out, buffer_39_out, buffer_40_out, buffer_42_out, buffer_43_out, buffer_44_out,
       buffer_76_out, buffer_78_out, buffer_79_out, buffer_84_out, buffer_109_out, button_1_out, C_____RAM,
       CLOCK, clock_1_out, COMMAND, comparator_1_lt, d_ff_1_q, d_ff_2_q, d_ff_3_q, d_ff_4_q, d_ff_5_q,
       d_ff_6_q, d_ff_7_q, d_ff_8_q, d_ff_9_q, d_ff_10_q, d_ff_11_q, d_ff_12_q, d_ff_13_q, d_ff_14_q,
       d_ff_15_q, d_ff_16_q, d_ff_17_q, d_ff_18_q, decoder_1_out0, decoder_1_out1, decoder_1_out2,
       decoder_1_out3, decoder_1_out4, decoder_1_out5, decoder_1_out6, decoder_1_out7, decoder_1_out8,
       decoder_1_out9, decoder_1_out10, decoder_1_out11, decoder_1_out12, decoder_1_out13, decoder_1_out14,
       decoder_1_out15, decoder_3_out0, decoder_3_out1, decoder_6_out0, decoder_6_out1, decoder_12_out0,
       decoder_12_out1, decoder_12_out2, decoder_13_out0, decoder_13_out1, decoder_13_out2, decoder_14_out0,
       decoder_14_out1, decoder_14_out2, decoder_15_out0, decoder_15_out2, decoder_15_out3, decoder_15_out4,
       decoder_18_out0, decoder_18_out1, decoder_18_out2, decoder_18_out3, decoder_18_out4, decoder_18_out5,
       decoder_18_out6, decoder_18_out7, decoder_18_out8, decoder_18_out9, decoder_18_out10,
       decoder_18_out11, decoder_18_out12, decoder_18_out13, decoder_18_out14, decoder_18_out15,
       INPUT_____RAM, JUMP, JUMPIF, LOAD_A, LOAD_B, LOAD_C, LOAD_CARACTER, LOAD_RAM, MUL_A___B, not_1_out,
       not_2_out, pull_resistor_1_node, pull_resistor_33_node, pull_resistor_34_node, pull_resistor_41_node,
       pull_resistor_46_node, pull_resistor_47_node, pull_resistor_48_node, pull_resistor_49_node,
       pull_resistor_50_node, pull_resistor_53_node, pull_resistor_56_node, pull_resistor_58_node, RAM_____A,
       RAM_____B, RAM_____C, RAM_____DISPLAY, ROM_____A, ROM_____B, ROM_____C, ROM_____RAM, SAVE_A, SAVE_B,
       SAVE_C, SAVE_CYCLE, SAVE_RAM, SCREEN_SAVE;
  wire [3:0] buffer_12_out, buffer_12_out_2, buffer_12_out_3, buffer_12_out_4;
  wire [6:0] INPUT_CARACTER;
  wire [15:0] A_____BUS, adder_1_out, adder_2_out, B_____BUS, buffer_1_out, buffer_3_out, buffer_5_out,
       buffer_8_out, buffer_30_out, buffer_81_out, buffer_107_out, buffer_108_out, BUS_____A, BUS_____B,
       BUS_____C, C_____BUS, CLOCK_CYCLE, controlled_buffer_4_out, controlled_buffer_17_out,
       controlled_buffer_35_out, controlled_buffer_36_out, controlled_buffer_37_out,
       controlled_buffer_38_out, controlled_buffer_39_out, controlled_buffer_40_out,
       controlled_buffer_41_out, controlled_buffer_42_out, controlled_buffer_43_out,
       controlled_buffer_44_out, controlled_buffer_45_out, controlled_buffer_46_out,
       controlled_buffer_47_out, controlled_buffer_48_out, controlled_buffer_49_out,
       controlled_buffer_50_out, controlled_buffer_51_out, multiplier_1_out, PROVE, pull_resistor_32_node,
       pull_resistor_59_node, RAM_____BUS, RAM_ADDRESS, RAM_DATA, register_1_q, register_2_q, register_3_q,
       register_6_q, register_7_q, rom_1_data, ROM_____BUS, SCREEN_1, SCREEN_2, SCREEN_3, SCREEN_4, SCREEN_5,
       SCREEN_6, SCREEN_7, SCREEN_8, SCREEN_9, SCREEN_10, SCREEN_11, SCREEN_12, SCREEN_13, SCREEN_14,
       SCREEN_15, SCREEN_16, SCREEN_DATA, SCREEN_SECTOR, tunnel;

  assign buffer_1_out = BUS_____A;  // Buffer buffer_1, 16 bits wide
  buf buffer_2 (buffer_2_out, SAVE_A);
  assign buffer_3_out = BUS_____B;  // Buffer buffer_3, 16 bits wide
  buf buffer_4 (buffer_4_out, SAVE_B);
  assign buffer_5_out = BUS_____C;  // Buffer buffer_5, 16 bits wide
  buf buffer_6 (buffer_6_out, SAVE_C);
  not not_1 (not_1_out, pull_resistor_1_node);
  Pull_Resistor pull_resistor_1 (.node(pull_resistor_1_node));
  buf buffer_7 (pull_resistor_1_node, COMMAND);
  and and_1 (and_1_out, in_1, not_1_out);
  Decoder #(.select(4)) decoder_1 (
    .out0(decoder_1_out0), .out1(decoder_1_out1), .out2(decoder_1_out2), .out3(decoder_1_out3),
    .out4(decoder_1_out4), .out5(decoder_1_out5), .out6(decoder_1_out6), .out7(decoder_1_out7),
    .out8(decoder_1_out8), .out9(decoder_1_out9), .out10(decoder_1_out10), .out11(decoder_1_out11),
    .out12(decoder_1_out12), .out13(decoder_1_out13), .out14(decoder_1_out14), .out15(decoder_1_out15),
    .sel(buffer_12_out_2), .en(and_1_out));
  assign buffer_8_out = PROVE;  // Buffer buffer_8, 16 bits wide
  // Probe on buffer_8_out
  Pull_Resistor pull_resistor_2 (.node(buffer_1_out));
  Register #(.width(16), .trigger("high")) register_1 (
    .D(buffer_1_out), .Q(register_1_q), .clk(buffer_2_out));  // open: en, clr
  Pull_Resistor pull_resistor_3 (.node(buffer_2_out));
  Pull_Resistor pull_resistor_4 (.node(buffer_3_out));
  Register #(.width(16), .trigger("high")) register_2 (
    .D(buffer_3_out), .Q(register_2_q), .clk(buffer_4_out));  // open: en, clr
  Pull_Resistor pull_resistor_5 (.node(buffer_4_out));
  Register #(.width(16), .trigger("high")) register_3 (
    .D(buffer_5_out), .Q(register_3_q), .clk(buffer_6_out));  // open: en, clr
  Pull_Resistor pull_resistor_6 (.node(buffer_5_out));
  Pull_Resistor pull_resistor_7 (.node(buffer_6_out));
  assign A_____BUS = buffer_9_out ? register_1_q : 16'bz;  // Controlled_Buffer controlled_buffer_1
  Pull_Resistor pull_resistor_8 (.node(A_____BUS));
  buf buffer_9 (buffer_9_out, LOAD_A);
  Pull_Resistor pull_resistor_9 (.node(buffer_9_out));
  Pull_Resistor pull_resistor_10 (.node(B_____BUS));
  assign B_____BUS = buffer_10_out ? register_2_q : 16'bz;  // Controlled_Buffer controlled_buffer_2
  buf buffer_10 (buffer_10_out, LOAD_B);
  Pull_Resistor pull_resistor_11 (.node(buffer_10_out));
  Pull_Resistor pull_resistor_12 (.node(C_____BUS));
  assign C_____BUS = buffer_11_out ? register_3_q : 16'bz;  // Controlled_Buffer controlled_buffer_3
  buf buffer_11 (buffer_11_out, LOAD_C);
  Pull_Resistor pull_resistor_13 (.node(buffer_11_out));
  LED led_1 (.in(not_1_out));
  assign {buffer_12_out_4, buffer_12_out_3, buffer_12_out_2, buffer_12_out} = ROM_____BUS;  // Buffer buffer_12, 16 bits wide
  Pull_Resistor pull_resistor_14 (.node({buffer_12_out_4, buffer_12_out_3, buffer_12_out_2, buffer_12_out}));
  Decoder #(.select(4)) decoder_2 (
    .sel(buffer_12_out), .en(decoder_1_out0));  // open: out0, out1, out2, out3, out4, out5, out6, out7, out8, out9, out10, out11, out12, out13, out14, out15
  Pull_Resistor pull_resistor_15 (.node(decoder_1_out0));
  Pull_Resistor pull_resistor_16 (.node(decoder_1_out1));
  Decoder #(.select(4)) decoder_3 (
    .out0(decoder_3_out0), .out1(decoder_3_out1), .sel(buffer_12_out), .en(decoder_1_out1));  // open: out2, out3, out4, out5, out6, out7, out8, out9, out10, out11, out12, out13, out14, out15
  Decoder #(.select(4)) decoder_4 (
    .sel(buffer_12_out), .en(decoder_1_out2));  // open: out0, out1, out2, out3, out4, out5, out6, out7, out8, out9, out10, out11, out12, out13, out14, out15
  Pull_Resistor pull_resistor_17 (.node(decoder_1_out2));
  Pull_Resistor pull_resistor_18 (.node(decoder_1_out3));
  Decoder #(.select(4)) decoder_5 (
    .sel(buffer_12_out), .en(decoder_1_out3));  // open: out0, out1, out2, out3, out4, out5, out6, out7, out8, out9, out10, out11, out12, out13, out14, out15
  Decoder #(.select(4)) decoder_6 (
    .out0(decoder_6_out0), .out1(decoder_6_out1), .sel(buffer_12_out), .en(decoder_1_out4));  // open: out2, out3, out4, out5, out6, out7, out8, out9, out10, out11, out12, out13, out14, out15
  Pull_Resistor pull_resistor_19 (.node(decoder_1_out4));
  Decoder #(.select(4)) decoder_7 (
    .sel(buffer_12_out), .en(decoder_1_out5));  // open: out0, out1, out2, out3, out4, out5, out6, out7, out8, out9, out10, out11, out12, out13, out14, out15
  Pull_Resistor pull_resistor_20 (.node(decoder_1_out5));
  Decoder #(.select(4)) decoder_8 (
    .sel(buffer_12_out), .en(decoder_1_out6));  // open: out0, out1, out2, out3, out4, out5, out6, out7, out8, out9, out10, out11, out12, out13, out14, out15
  Pull_Resistor pull_resistor_21 (.node(decoder_1_out6));
  Decoder #(.select(4)) decoder_9 (
    .sel(buffer_12_out), .en(decoder_1_out7));  // open: out0, out1, out2, out3, out4, out5, out6, out7, out8, out9, out10, out11, out12, out13, out14, out15
  Pull_Resistor pull_resistor_22 (.node(decoder_1_out7));
  Pull_Resistor pull_resistor_23 (.node(decoder_1_out8));
  Decoder #(.select(4)) decoder_10 (
    .sel(buffer_12_out), .en(decoder_1_out8));  // open: out0, out1, out2, out3, out4, out5, out6, out7, out8, out9, out10, out11, out12, out13, out14, out15
  Pull_Resistor pull_resistor_24 (.node(decoder_1_out9));
  Decoder #(.select(4)) decoder_11 (
    .sel(buffer_12_out), .en(decoder_1_out9));  // open: out0, out1, out2, out3, out4, out5, out6, out7, out8, out9, out10, out11, out12, out13, out14, out15
  Pull_Resistor pull_resistor_25 (.node(decoder_1_out10));
  Decoder #(.select(4)) decoder_12 (
    .out0(decoder_12_out0), .out1(decoder_12_out1), .out2(decoder_12_out2), .sel(buffer_12_out),
    .en(decoder_1_out10));  // open: out3, out4, out5, out6, out7, out8, out9, out10, out11, out12, out13, out14, out15
  Pull_Resistor pull_resistor_26 (.node(decoder_1_out11));
  Decoder #(.select(4)) decoder_13 (
    .out0(decoder_13_out0), .out1(decoder_13_out1), .out2(decoder_13_out2), .sel(buffer_12_out),
    .en(decoder_1_out11));  // open: out3, out4, out5, out6, out7, out8, out9, out10, out11, out12, out13, out14, out15
  Decoder #(.select(4)) decoder_14 (
    .out0(decoder_14_out0), .out1(decoder_14_out1), .out2(decoder_14_out2), .sel(buffer_12_out),
    .en(decoder_1_out12));  // open: out3, out4, out5, out6, out7, out8, out9, out10, out11, out12, out13, out14, out15
  Pull_Resistor pull_resistor_27 (.node(decoder_1_out12));
  Decoder #(.select(4)) decoder_15 (
    .out0(decoder_15_out0), .out2(decoder_15_out2), .out3(decoder_15_out3), .out4(decoder_15_out4),
    .sel(buffer_12_out), .en(decoder_1_out13));  // open: out1, out5, out6, out7, out8, out9, out10, out11, out12, out13, out14, out15
  Pull_Resistor pull_resistor_28 (.node(decoder_1_out13));
  Pull_Resistor pull_resistor_29 (.node(decoder_1_out14));
  Decoder #(.select(4)) decoder_16 (
    .sel(buffer_12_out), .en(decoder_1_out14));  // open: out0, out1, out2, out3, out4, out5, out6, out7, out8, out9, out10, out11, out12, out13, out14, out15
  Pull_Resistor pull_resistor_30 (.node(decoder_1_out15));
  Decoder #(.select(4)) decoder_17 (
    .sel(buffer_12_out), .en(decoder_1_out15));  // open: out0, out1, out2, out3, out4, out5, out6, out7, out8, out9, out10, out11, out12, out13, out14, out15
  and and_2 (CLOCK, in_1, clock_1_out);
  Clock clock_1 (.out(clock_1_out));
  buf buffer_13 (JUMP, decoder_3_out0);
  buf buffer_14 (JUMPIF, decoder_3_out1);
  buf buffer_15 (ADD_A___B, decoder_6_out0);
  buf buffer_16 (MUL_A___B, decoder_6_out1);
  buf buffer_17 (ROM_____A, decoder_12_out0);
  buf buffer_18 (RAM_____A, decoder_12_out1);
  buf buffer_19 (A_____RAM, decoder_12_out2);
  buf buffer_20 (ROM_____B, decoder_13_out0);
  buf buffer_21 (RAM_____B, decoder_13_out1);
  buf buffer_22 (B_____RAM, decoder_13_out2);
  buf buffer_23 (ROM_____C, decoder_14_out0);
  buf buffer_24 (RAM_____B, decoder_14_out1);
  buf buffer_25 (C_____RAM, decoder_14_out2);
  buf buffer_26 (ROM_____RAM, decoder_15_out0);
  buf buffer_27 (RAM_____DISPLAY, decoder_15_out2);
  buf buffer_28 (INPUT_____RAM, decoder_15_out3);
  buf buffer_29 (A_____PROVE, decoder_15_out4);
  assign buffer_30_out = RAM_ADDRESS;  // Buffer buffer_30, 16 bits wide
  Pull_Resistor pull_resistor_31 (.node(buffer_30_out));
  Pull_Resistor pull_resistor_32 (.node(pull_resistor_32_node));
  assign pull_resistor_32_node = RAM_DATA;  // Buffer buffer_31, 16 bits wide
  Pull_Resistor pull_resistor_33 (.node(pull_resistor_33_node));
  buf buffer_32 (pull_resistor_33_node, SAVE_RAM);
  DotMatrix #(.inputtype("row"), .matrixcols(16), .matrixrows(16)) dotmatrix_1 (
    .row0(SCREEN_1), .row1(SCREEN_2), .row2(SCREEN_3), .row3(SCREEN_4), .row4(SCREEN_5), .row5(SCREEN_6),
    .row6(SCREEN_7), .row7(SCREEN_8), .row8(SCREEN_9), .row9(SCREEN_10), .row10(SCREEN_11),
    .row11(SCREEN_12), .row12(SCREEN_13), .row13(SCREEN_14), .row14(SCREEN_15), .row15(SCREEN_16));
  // Probe on tunnel
  // Probe on tunnel
  Pull_Resistor pull_resistor_34 (.node(pull_resistor_34_node));
  buf buffer_33 (pull_resistor_34_node, LOAD_RAM);
  RAM #(.addrWidth(16), .dataWidth(16), .bus("separate")) ram_1 (
    .addr(buffer_30_out), .din(pull_resistor_32_node), .data(RAM_____BUS), .str(pull_resistor_33_node),
    .clk(CLOCK), .ld(pull_resistor_34_node));  // open: sel, clr
  // Probe on rom_1_data
  // Probe on rom_1_data
  ROM #(.addrWidth(16), .dataWidth(16)) rom_1 (.addr(tunnel), .data(rom_1_data));  // open: sel
  assign ROM_____BUS = rom_1_data;  // Buffer buffer_34, 16 bits wide
  buf buffer_35 (buffer_35_out, LOAD_CARACTER);
  Pull_Resistor pull_resistor_35 (.node(buffer_35_out));
  Keyboard #(.buflen(128)) keyboard_1 (
    .clk(buffer_35_out), .re(1'b1), .clr(button_1_out), .data(INPUT_CARACTER));  // open: avail
  Button button_1 (.out(button_1_out));
  // Probe on tunnel
  buf buffer_36 (buffer_36_out, SAVE_CYCLE);
  Pull_Resistor pull_resistor_36 (.node(buffer_36_out));
  not not_2 (not_2_out, buffer_36_out);
  assign controlled_buffer_4_out = buffer_36_out ? CLOCK_CYCLE : 16'bz;  // Controlled_Buffer controlled_buffer_4
  assign controlled_buffer_4_out = not_2_out ? adder_1_out : 16'bz;  // Controlled_Buffer controlled_buffer_5
  Pull_Resistor pull_resistor_37 (.node(controlled_buffer_4_out));
  Adder #(.width(16)) adder_1 (.a(tunnel), .b(16'h1), .out(adder_1_out));  // open: cin, cout
  Register #(.width(16)) register_4 (.D(controlled_buffer_4_out), .Q(tunnel), .clk(CLOCK));  // open: en, clr
  buf buffer_37 (buffer_37_out, JUMPIF);
  D_Flip_Flop d_ff_1 (.clk(CLOCK), .D(buffer_38_out), .Q(d_ff_1_q));  // open: Qn, preset, en, reset
  buf buffer_38 (buffer_38_out, A_____RAM);
  Pull_Resistor pull_resistor_38 (.node(buffer_38_out));
  assign RAM_ADDRESS = d_ff_1_q ? ROM_____BUS : 16'bz;  // Controlled_Buffer controlled_buffer_6
  assign RAM_DATA = d_ff_1_q ? A_____BUS : 16'bz;  // Controlled_Buffer controlled_buffer_7
  D_Flip_Flop d_ff_2 (.clk(CLOCK), .D(buffer_39_out), .Q(d_ff_2_q));  // open: Qn, preset, en, reset
  buf buffer_39 (buffer_39_out, B_____RAM);
  Pull_Resistor pull_resistor_39 (.node(buffer_39_out));
  assign RAM_ADDRESS = d_ff_2_q ? ROM_____BUS : 16'bz;  // Controlled_Buffer controlled_buffer_8
  assign RAM_DATA = d_ff_2_q ? B_____BUS : 16'bz;  // Controlled_Buffer controlled_buffer_9
  D_Flip_Flop d_ff_3 (.clk(CLOCK), .D(buffer_40_out), .Q(d_ff_3_q));  // open: Qn, preset, en, reset
  buf buffer_40 (buffer_40_out, C_____RAM);
  Pull_Resistor pull_resistor_40 (.node(buffer_40_out));
  assign RAM_ADDRESS = d_ff_3_q ? ROM_____BUS : 16'bz;  // Controlled_Buffer controlled_buffer_10
  assign RAM_DATA = d_ff_3_q ? C_____BUS : 16'bz;  // Controlled_Buffer controlled_buffer_11
  D_Flip_Flop d_ff_4 (.clk(CLOCK), .D(pull_resistor_41_node), .Q(d_ff_4_q));  // open: Qn, preset, en, reset
  Pull_Resistor pull_resistor_41 (.node(pull_resistor_41_node));
  buf buffer_41 (pull_resistor_41_node, ROM_____A);
  assign BUS_____A = d_ff_4_q ? ROM_____BUS : 16'bz;  // Controlled_Buffer controlled_buffer_12
  D_Flip_Flop d_ff_5 (.clk(CLOCK), .D(buffer_42_out), .Q(d_ff_5_q));  // open: Qn, preset, en, reset
  buf buffer_42 (buffer_42_out, ROM_____B);
  Pull_Resistor pull_resistor_42 (.node(buffer_42_out));
  assign BUS_____B = d_ff_5_q ? ROM_____BUS : 16'bz;  // Controlled_Buffer controlled_buffer_13
  D_Flip_Flop d_ff_6 (.clk(CLOCK), .D(buffer_43_out), .Q(d_ff_6_q));  // open: Qn, preset, en, reset
  buf buffer_43 (buffer_43_out, ROM_____C);
  Pull_Resistor pull_resistor_43 (.node(buffer_43_out));
  assign BUS_____C = d_ff_6_q ? ROM_____BUS : 16'bz;  // Controlled_Buffer controlled_buffer_14
  buf buffer_44 (buffer_44_out, ADD_A___B);
  Pull_Resistor pull_resistor_44 (.node(buffer_44_out));
  Adder #(.width(16)) adder_2 (.a(A_____BUS), .b(B_____BUS), .out(adder_2_out));  // open: cin, cout
  assign BUS_____C = buffer_44_out ? adder_2_out : 16'bz;  // Controlled_Buffer controlled_buffer_15
  D_Flip_Flop d_ff_7 (.clk(CLOCK), .D(buffer_37_out), .Q(d_ff_7_q));  // open: Qn, preset, en, reset
  Pull_Resistor pull_resistor_45 (.node(buffer_37_out));
  assign RAM_ADDRESS = d_ff_7_q ? ROM_____BUS : 16'bz;  // Controlled_Buffer controlled_buffer_16
  assign controlled_buffer_17_out = d_ff_7_q ? RAM_____BUS : 16'bz;  // Controlled_Buffer controlled_buffer_17
  D_Flip_Flop d_ff_8 (.clk(CLOCK), .D(pull_resistor_46_node), .Q(d_ff_8_q));  // open: Qn, preset, en, reset
  Pull_Resistor pull_resistor_46 (.node(pull_resistor_46_node));
  assign CLOCK_CYCLE = d_ff_8_q ? ROM_____BUS : 16'bz;  // Controlled_Buffer controlled_buffer_18
  D_Flip_Flop d_ff_9 (.clk(CLOCK), .D(pull_resistor_47_node), .Q(d_ff_9_q));  // open: Qn, preset, en, reset
  Pull_Resistor pull_resistor_47 (.node(pull_resistor_47_node));
  Register #(.width(16), .trigger("high")) register_5 (
    .D(A_____BUS), .Q(PROVE), .clk(pull_resistor_48_node));  // open: en, clr
  Pull_Resistor pull_resistor_48 (.node(pull_resistor_48_node));
  buf buffer_45 (pull_resistor_48_node, A_____PROVE);
  D_Flip_Flop d_ff_10 (.clk(CLOCK), .D(pull_resistor_49_node), .Q(d_ff_10_q));  // open: Qn, preset, en, reset
  Pull_Resistor pull_resistor_49 (.node(pull_resistor_49_node));
  buf buffer_46 (pull_resistor_49_node, INPUT_____RAM);
  assign RAM_ADDRESS = d_ff_10_q ? ROM_____BUS : 16'bz;  // Controlled_Buffer controlled_buffer_19
  assign RAM_DATA = d_ff_10_q ? {{9{1'b0}}, INPUT_CARACTER} : 16'bz;  // Controlled_Buffer controlled_buffer_20
  buf buffer_47 (LOAD_A, d_ff_1_q);
  buf buffer_48 (COMMAND, d_ff_1_q);
  buf buffer_49 (SAVE_RAM, d_ff_1_q);
  buf buffer_50 (LOAD_B, d_ff_2_q);
  buf buffer_51 (COMMAND, d_ff_2_q);
  buf buffer_52 (SAVE_RAM, d_ff_2_q);
  buf buffer_53 (LOAD_C, d_ff_3_q);
  buf buffer_54 (COMMAND, d_ff_3_q);
  buf buffer_55 (SAVE_RAM, d_ff_3_q);
  buf buffer_56 (SAVE_A, d_ff_4_q);
  buf buffer_57 (COMMAND, d_ff_4_q);
  buf buffer_58 (SAVE_B, d_ff_5_q);
  buf buffer_59 (COMMAND, d_ff_5_q);
  buf buffer_60 (SAVE_C, d_ff_6_q);
  buf buffer_61 (COMMAND, d_ff_6_q);
  buf buffer_62 (LOAD_A, buffer_44_out);
  buf buffer_63 (LOAD_B, buffer_44_out);
  buf buffer_64 (SAVE_C, buffer_44_out);
  buf buffer_65 (LOAD_RAM, d_ff_7_q);
  buf buffer_66 (COMMAND, d_ff_7_q);
  buf buffer_67 (LOAD_A, d_ff_7_q);
  Pull_Resistor pull_resistor_50 (.node(pull_resistor_50_node));
  Comparator #(.width(16)) comparator_1 (
    .a(controlled_buffer_17_out), .b(A_____BUS), .gt(pull_resistor_50_node), .eq(pull_resistor_46_node),
    .lt(comparator_1_lt));
  Pull_Resistor pull_resistor_51 (.node(comparator_1_lt));
  buf buffer_68 (SAVE_CYCLE, d_ff_8_q);
  buf buffer_69 (COMMAND, d_ff_8_q);
  buf buffer_70 (COMMAND, d_ff_9_q);
  buf buffer_71 (LOAD_A, pull_resistor_48_node);
  buf buffer_72 (LOAD_CARACTER, d_ff_10_q);
  buf buffer_73 (COMMAND, d_ff_10_q);
  buf buffer_74 (SAVE_RAM, d_ff_10_q);
  buf buffer_75 (COMMAND, pull_resistor_47_node);
  or or_1 (pull_resistor_47_node, pull_resistor_50_node, comparator_1_lt);
  buf buffer_76 (buffer_76_out, RAM_____A);
  Pull_Resistor pull_resistor_52 (.node(buffer_76_out));
  Pull_Resistor pull_resistor_53 (.node(pull_resistor_53_node));
  buf buffer_77 (pull_resistor_53_node, RAM_____B);
  buf buffer_78 (buffer_78_out, RAM_____C);
  Pull_Resistor pull_resistor_54 (.node(buffer_78_out));
  buf buffer_79 (buffer_79_out, JUMP);
  Pull_Resistor pull_resistor_55 (.node(buffer_79_out));
  Pull_Resistor pull_resistor_56 (.node(pull_resistor_56_node));
  buf buffer_80 (pull_resistor_56_node, RAM_____DISPLAY);
  assign buffer_81_out = RAM_____BUS;  // Buffer buffer_81, 16 bits wide
  Pull_Resistor pull_resistor_57 (.node(buffer_81_out));
  Pull_Resistor pull_resistor_58 (.node(pull_resistor_58_node));
  buf buffer_82 (pull_resistor_58_node, ROM_____RAM);
  Pull_Resistor pull_resistor_59 (.node(pull_resistor_59_node));
  assign pull_resistor_59_node = ROM_____BUS;  // Buffer buffer_83, 16 bits wide
  buf buffer_84 (buffer_84_out, MUL_A___B);
  buf buffer_85 (LOAD_RAM, d_ff_11_q);
  D_Flip_Flop d_ff_11 (.clk(CLOCK), .D(buffer_76_out), .Q(d_ff_11_q));  // open: Qn, preset, en, reset
  buf buffer_86 (COMMAND, d_ff_11_q);
  buf buffer_87 (SAVE_A, d_ff_11_q);
  assign RAM_ADDRESS = d_ff_11_q ? ROM_____BUS : 16'bz;  // Controlled_Buffer controlled_buffer_21
  assign BUS_____A = d_ff_11_q ? RAM_____BUS : 16'bz;  // Controlled_Buffer controlled_buffer_22
  buf buffer_88 (LOAD_RAM, d_ff_12_q);
  D_Flip_Flop d_ff_12 (.clk(CLOCK), .D(pull_resistor_53_node), .Q(d_ff_12_q));  // open: Qn, preset, en, reset
  buf buffer_89 (COMMAND, d_ff_12_q);
  buf buffer_90 (SAVE_B, d_ff_12_q);
  assign RAM_ADDRESS = d_ff_12_q ? ROM_____BUS : 16'bz;  // Controlled_Buffer controlled_buffer_23
  assign BUS_____B = d_ff_12_q ? RAM_____BUS : 16'bz;  // Controlled_Buffer controlled_buffer_24
  buf buffer_91 (LOAD_RAM, d_ff_13_q);
  buf buffer_92 (COMMAND, d_ff_13_q);
  D_Flip_Flop d_ff_13 (.clk(CLOCK), .D(buffer_78_out), .Q(d_ff_13_q));  // open: Qn, preset, en, reset
  buf buffer_93 (SAVE_C, d_ff_13_q);
  assign RAM_ADDRESS = d_ff_13_q ? ROM_____BUS : 16'bz;  // Controlled_Buffer controlled_buffer_25
  assign BUS_____C = d_ff_13_q ? RAM_____BUS : 16'bz;  // Controlled_Buffer controlled_buffer_26
  D_Flip_Flop d_ff_14 (.clk(CLOCK), .D(buffer_79_out), .Q(d_ff_14_q));  // open: Qn, preset, en, reset
  buf buffer_94 (SAVE_CYCLE, d_ff_14_q);
  buf buffer_95 (COMMAND, d_ff_14_q);
  assign CLOCK_CYCLE = d_ff_14_q ? ROM_____BUS : 16'bz;  // Controlled_Buffer controlled_buffer_27
  D_Flip_Flop d_ff_15 (.clk(CLOCK), .D(pull_resistor_56_node), .Q(d_ff_15_q));  // open: Qn, preset, en, reset
  buf buffer_96 (COMMAND, d_ff_15_q);
  buf buffer_97 (LOAD_RAM, d_ff_15_q);
  assign RAM_ADDRESS = d_ff_15_q ? ROM_____BUS : 16'bz;  // Controlled_Buffer controlled_buffer_28
  Register #(.width(16), .trigger("high")) register_6 (
    .D(buffer_81_out), .Q(register_6_q), .clk(d_ff_15_q));  // open: en, clr
  assign SCREEN_DATA = d_ff_16_q ? register_6_q : 16'bz;  // Controlled_Buffer controlled_buffer_29
  buf buffer_98 (LOAD_RAM, d_ff_16_q);
  D_Flip_Flop d_ff_16 (.clk(CLOCK), .D(d_ff_15_q), .Q(d_ff_16_q));  // open: Qn, preset, en, reset
  buf buffer_99 (SCREEN_SAVE, d_ff_16_q);
  buf buffer_100 (COMMAND, d_ff_16_q);
  assign RAM_ADDRESS = d_ff_16_q ? ROM_____BUS : 16'bz;  // Controlled_Buffer controlled_buffer_30
  assign SCREEN_SECTOR = d_ff_16_q ? RAM_____BUS : 16'bz;  // Controlled_Buffer controlled_buffer_31
  buf buffer_101 (COMMAND, d_ff_17_q);
  D_Flip_Flop d_ff_17 (.clk(CLOCK), .D(pull_resistor_58_node), .Q(d_ff_17_q));  // open: Qn, preset, en, reset
  Register #(.width(16), .trigger("high")) register_7 (
    .D(pull_resistor_59_node), .Q(register_7_q), .clk(d_ff_17_q));  // open: en, clr
  assign RAM_ADDRESS = d_ff_18_q ? register_7_q : 16'bz;  // Controlled_Buffer controlled_buffer_32
  buf buffer_102 (SAVE_RAM, d_ff_18_q);
  D_Flip_Flop d_ff_18 (.clk(CLOCK), .D(d_ff_17_q), .Q(d_ff_18_q));  // open: Qn, preset, en, reset
  buf buffer_103 (COMMAND, d_ff_18_q);
  assign RAM_DATA = d_ff_18_q ? ROM_____BUS : 16'bz;  // Controlled_Buffer controlled_buffer_33
  buf buffer_104 (LOAD_A, buffer_84_out);
  Pull_Resistor pull_resistor_60 (.node(buffer_84_out));
  buf buffer_105 (LOAD_B, buffer_84_out);
  buf buffer_106 (SAVE_C, buffer_84_out);
  Multiplier #(.width(16)) multiplier_1 (.a(A_____BUS), .b(B_____BUS), .out(multiplier_1_out));  // open: cin, cout
  assign BUS_____C = buffer_84_out ? multiplier_1_out : 16'bz;  // Controlled_Buffer controlled_buffer_34
  assign buffer_107_out = SCREEN_SECTOR;  // Buffer buffer_107, 16 bits wide
  assign buffer_108_out = SCREEN_DATA;  // Buffer buffer_108, 16 bits wide
  buf buffer_109 (buffer_109_out, SCREEN_SAVE);
  Decoder #(.select(4)) decoder_18 (
    .out0(decoder_18_out0), .out1(decoder_18_out1), .out2(decoder_18_out2), .out3(decoder_18_out3),
    .out4(decoder_18_out4), .out5(decoder_18_out5), .out6(decoder_18_out6), .out7(decoder_18_out7),
    .out8(decoder_18_out8), .out9(decoder_18_out9), .out10(decoder_18_out10), .out11(decoder_18_out11),
    .out12(decoder_18_out12), .out13(decoder_18_out13), .out14(decoder_18_out14), .out15(decoder_18_out15),
    .sel(buffer_107_out[3:0]), .en(buffer_109_out));
  Pull_Resistor pull_resistor_61 (.node(buffer_107_out[3:0]));
  assign controlled_buffer_35_out = buffer_109_out ? buffer_108_out : 16'bz;  // Controlled_Buffer controlled_buffer_35
  Pull_Resistor pull_resistor_62 (.node(controlled_buffer_35_out));
  Pull_Resistor pull_resistor_63 (.node(buffer_109_out));
  Pull_Resistor pull_resistor_64 (.node(decoder_18_out0));
  Pull_Resistor pull_resistor_65 (.node(decoder_18_out1));
  Pull_Resistor pull_resistor_66 (.node(decoder_18_out2));
  Pull_Resistor pull_resistor_67 (.node(decoder_18_out3));
  Pull_Resistor pull_resistor_68 (.node(decoder_18_out4));
  Pull_Resistor pull_resistor_69 (.node(decoder_18_out5));
  Pull_Resistor pull_resistor_70 (.node(decoder_18_out6));
  Pull_Resistor pull_resistor_71 (.node(decoder_18_out7));
  Pull_Resistor pull_resistor_72 (.node(decoder_18_out8));
  Pull_Resistor pull_resistor_73 (.node(decoder_18_out9));
  Pull_Resistor pull_resistor_74 (.node(decoder_18_out10));
  Pull_Resistor pull_resistor_75 (.node(decoder_18_out11));
  Pull_Resistor pull_resistor_76 (.node(decoder_18_out12));
  Pull_Resistor pull_resistor_77 (.node(decoder_18_out13));
  Pull_Resistor pull_resistor_78 (.node(decoder_18_out14));
  Pull_Resistor pull_resistor_79 (.node(decoder_18_out15));
  assign controlled_buffer_36_out = decoder_18_out0 ? controlled_buffer_35_out : 16'bz;  // Controlled_Buffer controlled_buffer_36
  Register #(.width(16), .trigger("high")) register_8 (
    .D(controlled_buffer_36_out), .Q(SCREEN_1));  // open: en, clk, clr
  Register #(.width(16), .trigger("falling")) register_9 (
    .D(controlled_buffer_37_out), .Q(SCREEN_2));  // open: en, clk, clr
  assign controlled_buffer_37_out = decoder_18_out1 ? controlled_buffer_35_out : 16'bz;  // Controlled_Buffer controlled_buffer_37
  assign controlled_buffer_38_out = decoder_18_out2 ? controlled_buffer_35_out : 16'bz;  // Controlled_Buffer controlled_buffer_38
  Register #(.width(16), .trigger("low")) register_10 (
    .D(controlled_buffer_38_out), .Q(SCREEN_3));  // open: en, clk, clr
  assign controlled_buffer_39_out = decoder_18_out3 ? controlled_buffer_35_out : 16'bz;  // Controlled_Buffer controlled_buffer_39
  Register #(.width(16), .trigger("high")) register_11 (
    .D(controlled_buffer_39_out), .Q(SCREEN_4));  // open: en, clk, clr
  assign controlled_buffer_40_out = decoder_18_out4 ? controlled_buffer_35_out : 16'bz;  // Controlled_Buffer controlled_buffer_40
  Register #(.width(16), .trigger("high")) register_12 (
    .D(controlled_buffer_40_out), .Q(SCREEN_5));  // open: en, clk, clr
  Register #(.width(16), .trigger("high")) register_13 (
    .D(controlled_buffer_41_out), .Q(SCREEN_6));  // open: en, clk, clr
  assign controlled_buffer_41_out = decoder_18_out5 ? controlled_buffer_35_out : 16'bz;  // Controlled_Buffer controlled_buffer_41
  Register #(.width(16), .trigger("high")) register_14 (
    .D(controlled_buffer_42_out), .Q(SCREEN_7));  // open: en, clk, clr
  assign controlled_buffer_42_out = decoder_18_out6 ? controlled_buffer_35_out : 16'bz;  // Controlled_Buffer controlled_buffer_42
  Register #(.width(16), .trigger("high")) register_15 (
    .D(controlled_buffer_43_out), .Q(SCREEN_8));  // open: en, clk, clr
  assign controlled_buffer_43_out = decoder_18_out7 ? controlled_buffer_35_out : 16'bz;  // Controlled_Buffer controlled_buffer_43
  Register #(.width(16), .trigger("high")) register_16 (
    .D(controlled_buffer_44_out), .Q(SCREEN_9));  // open: en, clk, clr
  assign controlled_buffer_44_out = decoder_18_out8 ? controlled_buffer_35_out : 16'bz;  // Controlled_Buffer controlled_buffer_44
  Register #(.width(16), .trigger("high")) register_17 (
    .D(controlled_buffer_45_out), .Q(SCREEN_10));  // open: en, clk, clr
  assign controlled_buffer_45_out = decoder_18_out9 ? controlled_buffer_35_out : 16'bz;  // Controlled_Buffer controlled_buffer_45
  Register #(.width(16), .trigger("high")) register_18 (
    .D(controlled_buffer_46_out), .Q(SCREEN_11));  // open: en, clk, clr
  assign controlled_buffer_46_out = decoder_18_out10 ? controlled_buffer_35_out : 16'bz;  // Controlled_Buffer controlled_buffer_46
  Register #(.width(16), .trigger("high")) register_19 (
    .D(controlled_buffer_47_out), .Q(SCREEN_12));  // open: en, clk, clr
  assign controlled_buffer_47_out = decoder_18_out11 ? controlled_buffer_35_out : 16'bz;  // Controlled_Buffer controlled_buffer_47
  Register #(.width(16), .trigger("high")) register_20 (
    .D(controlled_buffer_48_out), .Q(SCREEN_13));  // open: en, clk, clr
  assign controlled_buffer_48_out = decoder_18_out12 ? controlled_buffer_35_out : 16'bz;  // Controlled_Buffer controlled_buffer_48
  assign controlled_buffer_49_out = decoder_18_out13 ? controlled_buffer_35_out : 16'bz;  // Controlled_Buffer controlled_buffer_49
  Register #(.width(16), .trigger("high")) register_21 (
    .D(controlled_buffer_49_out), .Q(SCREEN_14));  // open: en, clk, clr
  Register #(.width(16), .trigger("high")) register_22 (
    .D(controlled_buffer_50_out), .Q(SCREEN_15));  // open: en, clk, clr
  assign controlled_buffer_50_out = decoder_18_out14 ? controlled_buffer_35_out : 16'bz;  // Controlled_Buffer controlled_buffer_50
  Register #(.width(16), .trigger("high")) register_23 (
    .D(controlled_buffer_51_out), .Q(SCREEN_16));  // open: en, clk, clr
  assign controlled_buffer_51_out = decoder_18_out15 ? controlled_buffer_35_out : 16'bz;  // Controlled_Buffer controlled_buffer_51

  // Notes on the sheet:
  //   buffer_13 drives only 1 and floats otherwise
  //   buffer_14 drives only 1 and floats otherwise
  //   buffer_15 drives only 1 and floats otherwise
  //   buffer_16 drives only 1 and floats otherwise
  //   buffer_17 drives only 1 and floats otherwise
  //   buffer_18 drives only 1 and floats otherwise
  //   buffer_19 drives only 1 and floats otherwise
  //   buffer_20 drives only 1 and floats otherwise
  //   buffer_21 drives only 1 and floats otherwise
  //   buffer_22 drives only 1 and floats otherwise
  //   buffer_23 drives only 1 and floats otherwise
  //   buffer_24 drives only 1 and floats otherwise
  //   buffer_25 drives only 1 and floats otherwise
  //   buffer_26 drives only 1 and floats otherwise
  //   buffer_27 drives only 1 and floats otherwise
  //   buffer_28 drives only 1 and floats otherwise
  //   buffer_29 drives only 1 and floats otherwise
  //   0
  //   1
  //   2
  //   3
  //   4
  //   5
  //   6
  //   7
  //   8
  //   9
  //   a
  //   b
  //   c
  //   d
  //   e
  //   f
  //   contents of rom_1 (hex, n*v repeats v):
  //   d0 1 1 d0 2 2 d0 3 3 d0 4 4 d0 5 5 d0 6 6 d0 7 7 d0 8 8 d0 9 9 d0 a a d0 b b d0 c c d0 d d d0 e e d0
  //   f f d0 6ff0 0 d0 6ff1 0 d0 6ff2 0 d0 6ff3 ff0 d0 6ff4 ff0 d0 6ff5 70 d0 6ff6 e0 d0 6ff7 1c0 d0 6ff8
  //   380 d0 6ff9 700 d0 6ffa e00 d0 6ffb ff0 d0 6ffc ff0 d0 6ffd 0 d0 6ffe 0 d0 6fff 0 d0 6fe0 0 d0 6fe1
  //   0 d0 6fe2 0 d0 6fe3 0 d0 6fe4 c30 d0 6fe5 e70 d0 6fe6 7e0 d0 6fe7 c30 d0 6fe8 180 d0 6fe9 180 d0
  //   6fea 180 d0 6feb 180 d0 6fec 180 d0 6fed 0 d0 6fee 0 d0 6fef 0 d0 6fd0 0 d0 6fd1 0 d0 6fd2 0 d0 6fd3
  //   0 d0 6fd4 c30 d0 6fd5 e70 d0 6fd6 7e0 d0 6fd7 c30 d0 6fd8 180 d0 6fd9 c30 d0 6fda 7e0 d0 6fdb e70 d0
  //   6fdc c30 d0 6fdd 0 d0 6fde 0 d0 6fdf 0 d0 6fc0 0 d0 6fc1 0 d0 6fc2 0 d0 6fc3 0 d0 6fc4 c30 d0 6fc5
  //   c30 d0 6fc6 c30 d0 6fc7 c30 d0 6fc8 c30 d0 6fc9 c30 d0 6fca d90 d0 6fcb ff0 d0 6fcc 660 d0 6fcd 0 d0
  //   6fce 0 d0 6fcf 0 d0 6fb0 0 d0 6fb1 0 d0 6fb2 0 d0 6fb3 c30 d0 6fb4 c30 d0 6fb5 c30 d0 6fb6 c30 d0
  //   6fb7 660 d0 6fb8 660 d0 6fb9 660 d0 6fba 660 d0 6fbb 3c0 d0 6fbc 3c0 d0 6fbd 0 d0 6fbe 0 d0 6fbf 0
  //   d2 6ff0 0 d2 6ff1 1 d2 6ff2 2 d2 6ff3 3 d2 6ff4 4 d2 6ff5 5 d2 6ff6 6 d2 6ff7 7 d2 6ff8 8 d2 6ff9 9
  //   d2 6ffa a d2 6ffb b d2 6ffc c d2 6ffd d d2 6ffe e d2 6fff f 10 11d
  //   buffer_34 drives only 1 and floats otherwise
  //   buffer_47 drives only 1 and floats otherwise
  //   buffer_48 drives only 1 and floats otherwise
  //   buffer_49 drives only 1 and floats otherwise
  //   buffer_50 drives only 1 and floats otherwise
  //   buffer_51 drives only 1 and floats otherwise
  //   buffer_52 drives only 1 and floats otherwise
  //   buffer_53 drives only 1 and floats otherwise
  //   buffer_54 drives only 1 and floats otherwise
  //   buffer_55 drives only 1 and floats otherwise
  //   buffer_56 drives only 1 and floats otherwise
  //   buffer_57 drives only 1 and floats otherwise
  //   buffer_58 drives only 1 and floats otherwise
  //   buffer_59 drives only 1 and floats otherwise
  //   buffer_60 drives only 1 and floats otherwise
  //   buffer_61 drives only 1 and floats otherwise
  //   buffer_62 drives only 1 and floats otherwise
  //   buffer_63 drives only 1 and floats otherwise
  //   buffer_64 drives only 1 and floats otherwise
  //   buffer_65 drives only 1 and floats otherwise
  //   buffer_66 drives only 1 and floats otherwise
  //   buffer_67 drives only 1 and floats otherwise
  //   buffer_68 drives only 1 and floats otherwise
  //   buffer_69 drives only 1 and floats otherwise
  //   buffer_70 drives only 1 and floats otherwise
  //   buffer_71 drives only 1 and floats otherwise
  //   buffer_72 drives only 1 and floats otherwise
  //   buffer_73 drives only 1 and floats otherwise
  //   buffer_74 drives only 1 and floats otherwise
  //   buffer_75 drives only 1 and floats otherwise
  //   buffer_85 drives only 1 and floats otherwise
  //   buffer_86 drives only 1 and floats otherwise
  //   buffer_87 drives only 1 and floats otherwise
  //   buffer_88 drives only 1 and floats otherwise
  //   buffer_89 drives only 1 and floats otherwise
  //   buffer_90 drives only 1 and floats otherwise
  //   buffer_91 drives only 1 and floats otherwise
  //   buffer_92 drives only 1 and floats otherwise
  //   buffer_93 drives only 1 and floats otherwise
  //   buffer_94 drives only 1 and floats otherwise
  //   buffer_95 drives only 1 and floats otherwise
  //   buffer_96 drives only 1 and floats otherwise
  //   buffer_97 drives only 1 and floats otherwise
  //   buffer_98 drives only 1 and floats otherwise
  //   buffer_99 drives only 1 and floats otherwise
  //   buffer_100 drives only 1 and floats otherwise
  //   buffer_101 drives only 1 and floats otherwise
  //   buffer_102 drives only 1 and floats otherwise
  //   buffer_103 drives only 1 and floats otherwise
  //   buffer_104 drives only 1 and floats otherwise
  //   buffer_105 drives only 1 and floats otherwise
  //   buffer_106 drives only 1 and floats otherwise
  //   SCRATCH PC ________________________________________________ SCRATCH PC _____________________________________________________SCRATCH PC ______________________________________________________SCRATCH PC________________________________________________________________ SCRATCH PC
endmodule
