// Logisim project PC.circ as structural Verilog: 1 circuit, main circuit main
module main (
  input  in_1
);

  wire A_____PROVE, A_____RAM, ADD_A___B, and_1_out, B_____RAM, buffer_2_out, buffer_4_out, buffer_6_out,
       buffer_7_out, buffer_10_out, buffer_11_out, buffer_34_out, buffer_36_out, buffer_40_out,
       buffer_41_out, buffer_67_out, buffer_68_out, buffer_70_out, buffer_73_out, C_____RAM, CLOCK,
       clock_1_out, COMMAND, comparator_1_eq, comparator_1_lt, d_ff_1_q, d_ff_2_q, d_ff_3_q, d_ff_4_q,
       d_ff_5_q, d_ff_6_q, d_ff_7_q, d_ff_8_q, d_ff_9_q, d_ff_10_q, d_ff_11_q, d_ff_12_q, d_ff_13_q,
       d_ff_14_q, d_ff_15_q, decoder_1_out0, decoder_1_out1, decoder_1_out2, decoder_1_out3, decoder_1_out4,
       decoder_1_out5, decoder_1_out6, decoder_1_out7, decoder_1_out8, decoder_1_out9, decoder_1_out10,
       decoder_1_out11, decoder_1_out12, decoder_1_out13, decoder_1_out14, decoder_1_out15, decoder_3_out0,
       decoder_3_out1, decoder_6_out0, decoder_12_out0, decoder_12_out1, decoder_12_out2, decoder_13_out0,
       decoder_13_out1, decoder_13_out2, decoder_14_out0, decoder_14_out1, decoder_14_out2, decoder_15_out0,
       decoder_15_out2, decoder_15_out4, decoder_18_out1, decoder_19_out0, decoder_19_out1, decoder_19_out2,
       decoder_19_out3, decoder_19_out4, decoder_19_out5, decoder_19_out6, decoder_19_out7, decoder_19_out8,
       decoder_19_out9, decoder_19_out10, decoder_19_out11, decoder_19_out12, decoder_19_out13,
       decoder_19_out14, decoder_19_out15, decoder_20_out0, decoder_20_out1, decoder_20_out2,
       decoder_20_out3, decoder_20_out4, decoder_20_out5, decoder_20_out6, decoder_20_out7, decoder_20_out8,
       decoder_20_out9, decoder_20_out10, decoder_20_out11, decoder_20_out12, decoder_20_out13,
       decoder_20_out14, decoder_20_out15, JUMP, JUMPIF, LOAD_A, LOAD_B, LOAD_C, LOAD_RAM, not_1_out,
       not_2_out, or_1_out, pull_resistor_9_node, pull_resistor_33_node, pull_resistor_34_node,
       pull_resistor_35_node, pull_resistor_37_node, pull_resistor_39_node, pull_resistor_40_node,
       pull_resistor_41_node, pull_resistor_44_node, pull_resistor_46_node, pull_resistor_51_node,
       pull_resistor_53_node, pull_resistor_58_node, pull_resistor_60_node, RAM_____A, RAM_____B, RAM_____C,
       RAM_____DISPLAY, ROM_____A, ROM_____B, ROM_____C, ROM_____RAM, SAVE_A, SAVE_B, SAVE_C, SAVE_CYCLE,
       SAVE_RAM, SCREEN_SAVE;
  wire [3:0] pull_resistor_14_node, pull_resistor_14_node_2;
  wire [7:0] A_____BUS, adder_1_out, adder_2_out, B_____BUS, buffer_1_out, buffer_3_out, buffer_5_out,
       buffer_8_out, buffer_29_out, buffer_72_out, buffer_74_out, buffer_95_out, BUS_____A, BUS_____B,
       BUS_____C, C_____BUS, CLOCK_CYCLE, controlled_buffer_4_out, controlled_buffer_17_out, PROVE,
       pull_resistor_31_node, pull_resistor_57_node, RAM_____BUS, RAM_ADDRESS, RAM_DATA, register_1_q,
       register_2_q, register_3_q, register_6_q, register_7_q, rom_1_data, ROM_____BUS, SCREEN_DATA,
       SCREEN_SECTOR, tunnel;
  wire [15:0] SCREEN_1, SCREEN_2, SCREEN_3, SCREEN_4, SCREEN_5, SCREEN_6, SCREEN_7, SCREEN_8, SCREEN_9,
       SCREEN_10, SCREEN_11, SCREEN_12, SCREEN_13, SCREEN_14, SCREEN_15, SCREEN_16;

  assign buffer_1_out = BUS_____A;  // Buffer buffer_1, 8 bits wide
  buf buffer_2 (buffer_2_out, SAVE_A);
  assign buffer_3_out = BUS_____B;  // Buffer buffer_3, 8 bits wide
  buf buffer_4 (buffer_4_out, SAVE_B);
  assign buffer_5_out = BUS_____C;  // Buffer buffer_5, 8 bits wide
  buf buffer_6 (buffer_6_out, SAVE_C);
  buf buffer_7 (buffer_7_out, COMMAND);
  Pull_Resistor pull_resistor_1 (.node(buffer_7_out));
  not not_1 (not_1_out, buffer_7_out);
  and and_1 (and_1_out, in_1, not_1_out);
  Decoder #(.select(4)) decoder_1 (
    .out0(decoder_1_out0), .out1(decoder_1_out1), .out2(decoder_1_out2), .out3(decoder_1_out3),
    .out4(decoder_1_out4), .out5(decoder_1_out5), .out6(decoder_1_out6), .out7(decoder_1_out7),
    .out8(decoder_1_out8), .out9(decoder_1_out9), .out10(decoder_1_out10), .out11(decoder_1_out11),
    .out12(decoder_1_out12), .out13(decoder_1_out13), .out14(decoder_1_out14), .out15(decoder_1_out15),
    .sel(pull_resistor_14_node_2), .en(and_1_out));
  Register #(.trigger("high")) register_1 (.D(buffer_1_out), .Q(register_1_q), .clk(buffer_2_out));  // open: en, clr
  Pull_Resistor pull_resistor_2 (.node(buffer_1_out));
  Pull_Resistor pull_resistor_3 (.node(buffer_2_out));
  Register #(.trigger("high")) register_2 (.D(buffer_3_out), .Q(register_2_q), .clk(buffer_4_out));  // open: en, clr
  Pull_Resistor pull_resistor_4 (.node(buffer_3_out));
  Pull_Resistor pull_resistor_5 (.node(buffer_4_out));
  Register #(.trigger("high")) register_3 (.D(buffer_5_out), .Q(register_3_q), .clk(buffer_6_out));  // open: en, clr
  Pull_Resistor pull_resistor_6 (.node(buffer_5_out));
  Pull_Resistor pull_resistor_7 (.node(buffer_6_out));
  // Probe on buffer_8_out
  assign buffer_8_out = PROVE;  // Buffer buffer_8, 8 bits wide
  Pull_Resistor pull_resistor_8 (.node(A_____BUS));
  assign A_____BUS = pull_resistor_9_node ? register_1_q : 8'bz;  // Controlled_Buffer controlled_buffer_1
  Pull_Resistor pull_resistor_9 (.node(pull_resistor_9_node));
  buf buffer_9 (pull_resistor_9_node, LOAD_A);
  Pull_Resistor pull_resistor_10 (.node(B_____BUS));
  assign B_____BUS = buffer_10_out ? register_2_q : 8'bz;  // Controlled_Buffer controlled_buffer_2
  buf buffer_10 (buffer_10_out, LOAD_B);
  Pull_Resistor pull_resistor_11 (.node(buffer_10_out));
  Pull_Resistor pull_resistor_12 (.node(C_____BUS));
  assign C_____BUS = buffer_11_out ? register_3_q : 8'bz;  // Controlled_Buffer controlled_buffer_3
  buf buffer_11 (buffer_11_out, LOAD_C);
  Pull_Resistor pull_resistor_13 (.node(buffer_11_out));
  Pull_Resistor pull_resistor_14 (.node({pull_resistor_14_node_2, pull_resistor_14_node}));
  assign {pull_resistor_14_node_2, pull_resistor_14_node} = ROM_____BUS;  // Buffer buffer_12, 8 bits wide
  Pull_Resistor pull_resistor_15 (.node(decoder_1_out0));
  Decoder #(.select(4)) decoder_2 (
    .sel(pull_resistor_14_node), .en(decoder_1_out0));  // open: out0, out1, out2, out3, out4, out5, out6, out7, out8, out9, out10, out11, out12, out13, out14, out15
  Pull_Resistor pull_resistor_16 (.node(decoder_1_out1));
  Decoder #(.select(4)) decoder_3 (
    .out0(decoder_3_out0), .out1(decoder_3_out1), .sel(pull_resistor_14_node), .en(decoder_1_out1));  // open: out2, out3, out4, out5, out6, out7, out8, out9, out10, out11, out12, out13, out14, out15
  Decoder #(.select(4)) decoder_4 (
    .sel(pull_resistor_14_node), .en(decoder_1_out2));  // open: out0, out1, out2, out3, out4, out5, out6, out7, out8, out9, out10, out11, out12, out13, out14, out15
  Pull_Resistor pull_resistor_17 (.node(decoder_1_out2));
  Decoder #(.select(4)) decoder_5 (
    .sel(pull_resistor_14_node), .en(decoder_1_out3));  // open: out0, out1, out2, out3, out4, out5, out6, out7, out8, out9, out10, out11, out12, out13, out14, out15
  Pull_Resistor pull_resistor_18 (.node(decoder_1_out3));
  Pull_Resistor pull_resistor_19 (.node(decoder_1_out4));
  Decoder #(.select(4)) decoder_6 (
    .out0(decoder_6_out0), .sel(pull_resistor_14_node), .en(decoder_1_out4));  // open: out1, out2, out3, out4, out5, out6, out7, out8, out9, out10, out11, out12, out13, out14, out15
  Decoder #(.select(4)) decoder_7 (
    .sel(pull_resistor_14_node), .en(decoder_1_out5));  // open: out0, out1, out2, out3, out4, out5, out6, out7, out8, out9, out10, out11, out12, out13, out14, out15
  Pull_Resistor pull_resistor_20 (.node(decoder_1_out5));
  Decoder #(.select(4)) decoder_8 (
    .sel(pull_resistor_14_node), .en(decoder_1_out6));  // open: out0, out1, out2, out3, out4, out5, out6, out7, out8, out9, out10, out11, out12, out13, out14, out15
  Pull_Resistor pull_resistor_21 (.node(decoder_1_out6));
  Pull_Resistor pull_resistor_22 (.node(decoder_1_out7));
  Decoder #(.select(4)) decoder_9 (
    .sel(pull_resistor_14_node), .en(decoder_1_out7));  // open: out0, out1, out2, out3, out4, out5, out6, out7, out8, out9, out10, out11, out12, out13, out14, out15
  Pull_Resistor pull_resistor_23 (.node(decoder_1_out8));
  Decoder #(.select(4)) decoder_10 (
    .sel(pull_resistor_14_node), .en(decoder_1_out8));  // open: out0, out1, out2, out3, out4, out5, out6, out7, out8, out9, out10, out11, out12, out13, out14, out15
  Pull_Resistor pull_resistor_24 (.node(decoder_1_out9));
  Decoder #(.select(4)) decoder_11 (
    .sel(pull_resistor_14_node), .en(decoder_1_out9));  // open: out0, out1, out2, out3, out4, out5, out6, out7, out8, out9, out10, out11, out12, out13, out14, out15
  Decoder #(.select(4)) decoder_12 (
    .out0(decoder_12_out0), .out1(decoder_12_out1), .out2(decoder_12_out2), .sel(pull_resistor_14_node),
    .en(decoder_1_out10));  // open: out3, out4, out5, out6, out7, out8, out9, out10, out11, out12, out13, out14, out15
  Pull_Resistor pull_resistor_25 (.node(decoder_1_out10));
  Pull_Resistor pull_resistor_26 (.node(decoder_1_out11));
  Decoder #(.select(4)) decoder_13 (
    .out0(decoder_13_out0), .out1(decoder_13_out1), .out2(decoder_13_out2), .sel(pull_resistor_14_node),
    .en(decoder_1_out11));  // open: out3, out4, out5, out6, out7, out8, out9, out10, out11, out12, out13, out14, out15
  Decoder #(.select(4)) decoder_14 (
    .out0(decoder_14_out0), .out1(decoder_14_out1), .out2(decoder_14_out2), .sel(pull_resistor_14_node),
    .en(decoder_1_out12));  // open: out3, out4, out5, out6, out7, out8, out9, out10, out11, out12, out13, out14, out15
  Pull_Resistor pull_resistor_27 (.node(decoder_1_out12));
  Pull_Resistor pull_resistor_28 (.node(decoder_1_out13));
  Decoder #(.select(4)) decoder_15 (
    .out0(decoder_15_out0), .out2(decoder_15_out2), .out4(decoder_15_out4), .sel(pull_resistor_14_node),
    .en(decoder_1_out13));  // open: out1, out3, out5, out6, out7, out8, out9, out10, out11, out12, out13, out14, out15
  Decoder #(.select(4)) decoder_16 (
    .sel(pull_resistor_14_node), .en(decoder_1_out14));  // open: out0, out1, out2, out3, out4, out5, out6, out7, out8, out9, out10, out11, out12, out13, out14, out15
  Pull_Resistor pull_resistor_29 (.node(decoder_1_out14));
  Pull_Resistor pull_resistor_30 (.node(decoder_1_out15));
  Decoder #(.select(4)) decoder_17 (
    .sel(pull_resistor_14_node), .en(decoder_1_out15));  // open: out0, out1, out2, out3, out4, out5, out6, out7, out8, out9, out10, out11, out12, out13, out14, out15
  buf buffer_13 (JUMP, decoder_3_out0);
  buf buffer_14 (JUMPIF, decoder_3_out1);
  buf buffer_15 (ADD_A___B, decoder_6_out0);
  buf buffer_16 (ROM_____A, decoder_12_out0);
  buf buffer_17 (RAM_____A, decoder_12_out1);
  buf buffer_18 (A_____RAM, decoder_12_out2);
  buf buffer_19 (ROM_____B, decoder_13_out0);
  buf buffer_20 (RAM_____B, decoder_13_out1);
  buf buffer_21 (B_____RAM, decoder_13_out2);
  buf buffer_22 (ROM_____C, decoder_14_out0);
  buf buffer_23 (RAM_____B, decoder_14_out1);
  buf buffer_24 (C_____RAM, decoder_14_out2);
  buf buffer_25 (ROM_____RAM, decoder_15_out0);
  buf buffer_26 (RAM_____DISPLAY, decoder_15_out2);
  buf buffer_27 (A_____PROVE, decoder_15_out4);
  Pull_Resistor pull_resistor_31 (.node(pull_resistor_31_node));
  assign pull_resistor_31_node = RAM_ADDRESS;  // Buffer buffer_28, 8 bits wide
  assign buffer_29_out = RAM_DATA;  // Buffer buffer_29, 8 bits wide
  Pull_Resistor pull_resistor_32 (.node(buffer_29_out));
  Pull_Resistor pull_resistor_33 (.node(pull_resistor_33_node));
  buf buffer_30 (pull_resistor_33_node, SAVE_RAM);
  DotMatrix #(.inputtype("row"), .matrixcols(16), .matrixrows(16)) dotmatrix_1 (
    .row0(SCREEN_1), .row1(SCREEN_2), .row2(SCREEN_3), .row3(SCREEN_4), .row4(SCREEN_5), .row5(SCREEN_6),
    .row6(SCREEN_7), .row7(SCREEN_8), .row8(SCREEN_9), .row9(SCREEN_10), .row10(SCREEN_11),
    .row11(SCREEN_12), .row12(SCREEN_13), .row13(SCREEN_14), .row14(SCREEN_15), .row15(SCREEN_16));
  and and_2 (CLOCK, in_1, clock_1_out);
  Clock clock_1 (.out(clock_1_out));
  // Probe on tunnel
  // Probe on tunnel
  Pull_Resistor pull_resistor_34 (.node(pull_resistor_34_node));
  buf buffer_31 (pull_resistor_34_node, LOAD_RAM);
  RAM #(.bus("separate")) ram_1 (
    .addr(pull_resistor_31_node), .din(buffer_29_out), .data(RAM_____BUS), .str(pull_resistor_33_node),
    .clk(CLOCK), .ld(pull_resistor_34_node));  // open: sel, clr
  // Probe on rom_1_data
  // Probe on rom_1_data
  assign ROM_____BUS = rom_1_data;  // Buffer buffer_32, 8 bits wide
  ROM rom_1 (.addr(tunnel), .data(rom_1_data));  // open: sel
  Pull_Resistor pull_resistor_35 (.node(pull_resistor_35_node));
  buf buffer_33 (pull_resistor_35_node, SAVE_CYCLE);
  assign controlled_buffer_4_out = pull_resistor_35_node ? CLOCK_CYCLE : 8'bz;  // Controlled_Buffer controlled_buffer_4
  // Probe on tunnel
  Adder adder_1 (.a(tunnel), .b(8'h1), .out(adder_1_out));  // open: cin, cout
  not not_2 (not_2_out, pull_resistor_35_node);
  assign controlled_buffer_4_out = not_2_out ? adder_1_out : 8'bz;  // Controlled_Buffer controlled_buffer_5
  Pull_Resistor pull_resistor_36 (.node(controlled_buffer_4_out));
  Register register_4 (.D(controlled_buffer_4_out), .Q(tunnel), .clk(CLOCK));  // open: en, clr
  buf buffer_34 (buffer_34_out, JUMPIF);
  Pull_Resistor pull_resistor_37 (.node(pull_resistor_37_node));
  buf buffer_35 (pull_resistor_37_node, A_____PROVE);
  D_Flip_Flop d_ff_1 (.clk(CLOCK), .D(buffer_36_out), .Q(d_ff_1_q));  // open: Qn, preset, en, reset
  buf buffer_36 (buffer_36_out, A_____RAM);
  Pull_Resistor pull_resistor_38 (.node(buffer_36_out));
  assign RAM_ADDRESS = d_ff_1_q ? ROM_____BUS : 8'bz;  // Controlled_Buffer controlled_buffer_6
  assign RAM_DATA = d_ff_1_q ? A_____BUS : 8'bz;  // Controlled_Buffer controlled_buffer_7
  D_Flip_Flop d_ff_2 (.clk(CLOCK), .D(pull_resistor_39_node), .Q(d_ff_2_q));  // open: Qn, preset, en, reset
  Pull_Resistor pull_resistor_39 (.node(pull_resistor_39_node));
  buf buffer_37 (pull_resistor_39_node, B_____RAM);
  assign RAM_ADDRESS = d_ff_2_q ? ROM_____BUS : 8'bz;  // Controlled_Buffer controlled_buffer_8
  assign RAM_DATA = d_ff_2_q ? B_____BUS : 8'bz;  // Controlled_Buffer controlled_buffer_9
  D_Flip_Flop d_ff_3 (.clk(CLOCK), .D(pull_resistor_40_node), .Q(d_ff_3_q));  // open: Qn, preset, en, reset
  Pull_Resistor pull_resistor_40 (.node(pull_resistor_40_node));
  buf buffer_38 (pull_resistor_40_node, C_____RAM);
  assign RAM_ADDRESS = d_ff_3_q ? ROM_____BUS : 8'bz;  // Controlled_Buffer controlled_buffer_10
  assign RAM_DATA = d_ff_3_q ? C_____BUS : 8'bz;  // Controlled_Buffer controlled_buffer_11
  D_Flip_Flop d_ff_4 (.clk(CLOCK), .D(pull_resistor_41_node), .Q(d_ff_4_q));  // open: Qn, preset, en, reset
  Pull_Resistor pull_resistor_41 (.node(pull_resistor_41_node));
  buf buffer_39 (pull_resistor_41_node, ROM_____A);
  assign BUS_____A = d_ff_4_q ? ROM_____BUS : 8'bz;  // Controlled_Buffer controlled_buffer_12
  D_Flip_Flop d_ff_5 (.clk(CLOCK), .D(buffer_40_out), .Q(d_ff_5_q));  // open: Qn, preset, en, reset
  buf buffer_40 (buffer_40_out, ROM_____B);
  Pull_Resistor pull_resistor_42 (.node(buffer_40_out));
  assign BUS_____B = d_ff_5_q ? ROM_____BUS : 8'bz;  // Controlled_Buffer controlled_buffer_13
  D_Flip_Flop d_ff_6 (.clk(CLOCK), .D(buffer_41_out), .Q(d_ff_6_q));  // open: Qn, preset, en, reset
  buf buffer_41 (buffer_41_out, ROM_____C);
  Pull_Resistor pull_resistor_43 (.node(buffer_41_out));
  assign BUS_____C = d_ff_6_q ? ROM_____BUS : 8'bz;  // Controlled_Buffer controlled_buffer_14
  Pull_Resistor pull_resistor_44 (.node(pull_resistor_44_node));
  buf buffer_42 (pull_resistor_44_node, ADD_A___B);
  assign BUS_____C = pull_resistor_44_node ? adder_2_out : 8'bz;  // Controlled_Buffer controlled_buffer_15
  Adder adder_2 (.a(A_____BUS), .b(B_____BUS), .out(adder_2_out));  // open: cin, cout
  D_Flip_Flop d_ff_7 (.clk(CLOCK), .D(buffer_34_out), .Q(d_ff_7_q));  // open: Qn, preset, en, reset
  Pull_Resistor pull_resistor_45 (.node(buffer_34_out));
  assign RAM_ADDRESS = d_ff_7_q ? ROM_____BUS : 8'bz;  // Controlled_Buffer controlled_buffer_16
  assign controlled_buffer_17_out = d_ff_7_q ? RAM_____BUS : 8'bz;  // Controlled_Buffer controlled_buffer_17
  Register #(.trigger("high")) register_5 (.D(A_____BUS), .Q(PROVE), .clk(pull_resistor_37_node));  // open: en, clr
  buf buffer_43 (LOAD_A, pull_resistor_37_node);
  buf buffer_44 (LOAD_A, d_ff_1_q);
  buf buffer_45 (COMMAND, d_ff_1_q);
  buf buffer_46 (SAVE_RAM, d_ff_1_q);
  buf buffer_47 (LOAD_B, d_ff_2_q);
  buf buffer_48 (COMMAND, d_ff_2_q);
  buf buffer_49 (SAVE_RAM, d_ff_2_q);
  buf buffer_50 (LOAD_C, d_ff_3_q);
  buf buffer_51 (COMMAND, d_ff_3_q);
  buf buffer_52 (SAVE_RAM, d_ff_3_q);
  buf buffer_53 (SAVE_A, d_ff_4_q);
  buf buffer_54 (COMMAND, d_ff_4_q);
  buf buffer_55 (SAVE_B, d_ff_5_q);
  buf buffer_56 (COMMAND, d_ff_5_q);
  buf buffer_57 (SAVE_C, d_ff_6_q);
  buf buffer_58 (COMMAND, d_ff_6_q);
  buf buffer_59 (LOAD_A, pull_resistor_44_node);
  buf buffer_60 (LOAD_B, pull_resistor_44_node);
  buf buffer_61 (SAVE_C, pull_resistor_44_node);
  buf buffer_62 (LOAD_RAM, d_ff_7_q);
  buf buffer_63 (COMMAND, d_ff_7_q);
  buf buffer_64 (LOAD_A, d_ff_7_q);
  Pull_Resistor pull_resistor_46 (.node(pull_resistor_46_node));
  Comparator comparator_1 (
    .a(controlled_buffer_17_out), .b(A_____BUS), .gt(pull_resistor_46_node), .eq(comparator_1_eq),
    .lt(comparator_1_lt));
  Pull_Resistor pull_resistor_47 (.node(comparator_1_lt));
  Pull_Resistor pull_resistor_48 (.node(comparator_1_eq));
  or or_1 (or_1_out, pull_resistor_46_node, comparator_1_lt);
  buf buffer_65 (COMMAND, or_1_out);
  buf buffer_66 (JUMP, comparator_1_eq);
  buf buffer_67 (buffer_67_out, RAM_____A);
  Pull_Resistor pull_resistor_49 (.node(buffer_67_out));
  buf buffer_68 (buffer_68_out, RAM_____B);
  Pull_Resistor pull_resistor_50 (.node(buffer_68_out));
  Pull_Resistor pull_resistor_51 (.node(pull_resistor_51_node));
  buf buffer_69 (pull_resistor_51_node, RAM_____C);
  buf buffer_70 (buffer_70_out, JUMP);
  Pull_Resistor pull_resistor_52 (.node(buffer_70_out));
  Pull_Resistor pull_resistor_53 (.node(pull_resistor_53_node));
  buf buffer_71 (pull_resistor_53_node, RAM_____DISPLAY);
  assign buffer_72_out = RAM_____BUS;  // Buffer buffer_72, 8 bits wide
  Pull_Resistor pull_resistor_54 (.node(buffer_72_out));
  buf buffer_73 (buffer_73_out, ROM_____RAM);
  Pull_Resistor pull_resistor_55 (.node(buffer_73_out));
  assign buffer_74_out = ROM_____BUS;  // Buffer buffer_74, 8 bits wide
  Pull_Resistor pull_resistor_56 (.node(buffer_74_out));
  buf buffer_75 (LOAD_RAM, d_ff_8_q);
  D_Flip_Flop d_ff_8 (.clk(CLOCK), .D(buffer_67_out), .Q(d_ff_8_q));  // open: Qn, preset, en, reset
  buf buffer_76 (COMMAND, d_ff_8_q);
  buf buffer_77 (SAVE_A, d_ff_8_q);
  assign RAM_ADDRESS = d_ff_8_q ? ROM_____BUS : 8'bz;  // Controlled_Buffer controlled_buffer_18
  assign BUS_____A = d_ff_8_q ? RAM_____BUS : 8'bz;  // Controlled_Buffer controlled_buffer_19
  buf buffer_78 (LOAD_RAM, d_ff_9_q);
  D_Flip_Flop d_ff_9 (.clk(CLOCK), .D(buffer_68_out), .Q(d_ff_9_q));  // open: Qn, preset, en, reset
  buf buffer_79 (COMMAND, d_ff_9_q);
  buf buffer_80 (SAVE_B, d_ff_9_q);
  assign RAM_ADDRESS = d_ff_9_q ? ROM_____BUS : 8'bz;  // Controlled_Buffer controlled_buffer_20
  assign BUS_____B = d_ff_9_q ? RAM_____BUS : 8'bz;  // Controlled_Buffer controlled_buffer_21
  buf buffer_81 (LOAD_RAM, d_ff_10_q);
  D_Flip_Flop d_ff_10 (.clk(CLOCK), .D(pull_resistor_51_node), .Q(d_ff_10_q));  // open: Qn, preset, en, reset
  buf buffer_82 (COMMAND, d_ff_10_q);
  buf buffer_83 (SAVE_C, d_ff_10_q);
  assign RAM_ADDRESS = d_ff_10_q ? ROM_____BUS : 8'bz;  // Controlled_Buffer controlled_buffer_22
  assign BUS_____C = d_ff_10_q ? RAM_____BUS : 8'bz;  // Controlled_Buffer controlled_buffer_23
  D_Flip_Flop d_ff_11 (.clk(CLOCK), .D(buffer_70_out), .Q(d_ff_11_q));  // open: Qn, preset, en, reset
  buf buffer_84 (SAVE_CYCLE, d_ff_11_q);
  buf buffer_85 (COMMAND, d_ff_11_q);
  assign CLOCK_CYCLE = d_ff_11_q ? ROM_____BUS : 8'bz;  // Controlled_Buffer controlled_buffer_24
  D_Flip_Flop d_ff_12 (.clk(CLOCK), .D(pull_resistor_53_node), .Q(d_ff_12_q));  // open: Qn, preset, en, reset
  buf buffer_86 (COMMAND, d_ff_12_q);
  buf buffer_87 (LOAD_RAM, d_ff_12_q);
  assign RAM_ADDRESS = d_ff_12_q ? ROM_____BUS : 8'bz;  // Controlled_Buffer controlled_buffer_25
  assign SCREEN_DATA = d_ff_13_q ? register_6_q : 8'bz;  // Controlled_Buffer controlled_buffer_26
  Register #(.trigger("high")) register_6 (.D(buffer_72_out), .Q(register_6_q), .clk(d_ff_12_q));  // open: en, clr
  buf buffer_88 (LOAD_RAM, d_ff_13_q);
  buf buffer_89 (SCREEN_SAVE, d_ff_13_q);
  D_Flip_Flop d_ff_13 (.clk(CLOCK), .D(d_ff_12_q), .Q(d_ff_13_q));  // open: Qn, preset, en, reset
  buf buffer_90 (COMMAND, d_ff_13_q);
  assign RAM_ADDRESS = d_ff_13_q ? ROM_____BUS : 8'bz;  // Controlled_Buffer controlled_buffer_27
  assign SCREEN_SECTOR = d_ff_13_q ? RAM_____BUS : 8'bz;  // Controlled_Buffer controlled_buffer_28
  buf buffer_91 (COMMAND, d_ff_14_q);
  D_Flip_Flop d_ff_14 (.clk(CLOCK), .D(buffer_73_out), .Q(d_ff_14_q));  // open: Qn, preset, en, reset
  assign RAM_ADDRESS = d_ff_15_q ? register_7_q : 8'bz;  // Controlled_Buffer controlled_buffer_29
  Register #(.trigger("high")) register_7 (.D(buffer_74_out), .Q(register_7_q), .clk(d_ff_14_q));  // open: en, clr
  buf buffer_92 (SAVE_RAM, d_ff_15_q);
  D_Flip_Flop d_ff_15 (.clk(CLOCK), .D(d_ff_14_q), .Q(d_ff_15_q));  // open: Qn, preset, en, reset
  buf buffer_93 (COMMAND, d_ff_15_q);
  assign RAM_DATA = d_ff_15_q ? ROM_____BUS : 8'bz;  // Controlled_Buffer controlled_buffer_30
  Pull_Resistor pull_resistor_57 (.node(pull_resistor_57_node));
  assign pull_resistor_57_node = SCREEN_SECTOR;  // Buffer buffer_94, 8 bits wide
  Pull_Resistor pull_resistor_58 (.node(pull_resistor_58_node));
  Decoder decoder_18 (
    .out0(pull_resistor_58_node), .out1(decoder_18_out1), .sel(pull_resistor_57_node[0]),
    .en(pull_resistor_60_node));
  Decoder #(.select(4)) decoder_19 (
    .out0(decoder_19_out0), .out1(decoder_19_out1), .out2(decoder_19_out2), .out3(decoder_19_out3),
    .out4(decoder_19_out4), .out5(decoder_19_out5), .out6(decoder_19_out6), .out7(decoder_19_out7),
    .out8(decoder_19_out8), .out9(decoder_19_out9), .out10(decoder_19_out10), .out11(decoder_19_out11),
    .out12(decoder_19_out12), .out13(decoder_19_out13), .out14(decoder_19_out14), .out15(decoder_19_out15),
    .sel(pull_resistor_57_node[4:1]), .en(pull_resistor_58_node));
  assign buffer_95_out = SCREEN_DATA;  // Buffer buffer_95, 8 bits wide
  Pull_Resistor pull_resistor_59 (.node(buffer_95_out));
  Pull_Resistor pull_resistor_60 (.node(pull_resistor_60_node));
  buf buffer_96 (pull_resistor_60_node, SCREEN_SAVE);
  Pull_Resistor pull_resistor_61 (.node(decoder_18_out1));
  Pull_Resistor pull_resistor_62 (.node(decoder_19_out0));
  Pull_Resistor pull_resistor_63 (.node(decoder_19_out1));
  Pull_Resistor pull_resistor_64 (.node(decoder_19_out2));
  Pull_Resistor pull_resistor_65 (.node(decoder_19_out3));
  Pull_Resistor pull_resistor_66 (.node(decoder_19_out4));
  Pull_Resistor pull_resistor_67 (.node(decoder_19_out5));
  Pull_Resistor pull_resistor_68 (.node(decoder_19_out6));
  Pull_Resistor pull_resistor_69 (.node(decoder_19_out7));
  Pull_Resistor pull_resistor_70 (.node(decoder_19_out8));
  Pull_Resistor pull_resistor_71 (.node(decoder_19_out9));
  Pull_Resistor pull_resistor_72 (.node(decoder_19_out10));
  Pull_Resistor pull_resistor_73 (.node(decoder_19_out11));
  Pull_Resistor pull_resistor_74 (.node(decoder_19_out12));
  Pull_Resistor pull_resistor_75 (.node(decoder_19_out13));
  Pull_Resistor pull_resistor_76 (.node(decoder_19_out14));
  Pull_Resistor pull_resistor_77 (.node(decoder_19_out15));
  Decoder #(.select(4)) decoder_20 (
    .out0(decoder_20_out0), .out1(decoder_20_out1), .out2(decoder_20_out2), .out3(decoder_20_out3),
    .out4(decoder_20_out4), .out5(decoder_20_out5), .out6(decoder_20_out6), .out7(decoder_20_out7),
    .out8(decoder_20_out8), .out9(decoder_20_out9), .out10(decoder_20_out10), .out11(decoder_20_out11),
    .out12(decoder_20_out12), .out13(decoder_20_out13), .out14(decoder_20_out14), .out15(decoder_20_out15),
    .sel(pull_resistor_57_node[4:1]), .en(decoder_18_out1));
  Register #(.trigger("high")) register_8 (
    .D(buffer_95_out), .en(decoder_19_out0), .Q(SCREEN_1[15:8]), .clk(pull_resistor_60_node));  // open: clr
  Register #(.trigger("high")) register_9 (
    .D(buffer_95_out), .en(decoder_19_out1), .Q(SCREEN_2[15:8]), .clk(pull_resistor_60_node));  // open: clr
  Register #(.trigger("high")) register_10 (
    .D(buffer_95_out), .en(decoder_19_out2), .Q(SCREEN_3[15:8]), .clk(pull_resistor_60_node));  // open: clr
  Register #(.trigger("high")) register_11 (
    .D(buffer_95_out), .en(decoder_19_out3), .Q(SCREEN_4[15:8]), .clk(pull_resistor_60_node));  // open: clr
  Register #(.trigger("high")) register_12 (
    .D(buffer_95_out), .en(decoder_19_out4), .Q(SCREEN_5[15:8]), .clk(pull_resistor_60_node));  // open: clr
  Register #(.trigger("high")) register_13 (
    .D(buffer_95_out), .en(decoder_19_out5), .Q(SCREEN_6[15:8]), .clk(pull_resistor_60_node));  // open: clr
  Register #(.trigger("high")) register_14 (
    .D(buffer_95_out), .en(decoder_19_out6), .Q(SCREEN_7[15:8]), .clk(pull_resistor_60_node));  // open: clr
  Register #(.trigger("high")) register_15 (
    .D(buffer_95_out), .en(decoder_19_out7), .Q(SCREEN_8[15:8]), .clk(pull_resistor_60_node));  // open: clr
  Register #(.trigger("high")) register_16 (
    .D(buffer_95_out), .en(decoder_19_out8), .Q(SCREEN_9[15:8]), .clk(pull_resistor_60_node));  // open: clr
  Register #(.trigger("high")) register_17 (
    .D(buffer_95_out), .en(decoder_19_out9), .Q(SCREEN_10[15:8]), .clk(pull_resistor_60_node));  // open: clr
  Register #(.trigger("high")) register_18 (
    .D(buffer_95_out), .en(decoder_19_out10), .Q(SCREEN_11[15:8]), .clk(pull_resistor_60_node));  // open: clr
  Register #(.trigger("high")) register_19 (
    .D(buffer_95_out), .en(decoder_19_out11), .Q(SCREEN_12[15:8]), .clk(pull_resistor_60_node));  // open: clr
  Register #(.trigger("high")) register_20 (
    .D(buffer_95_out), .en(decoder_19_out12), .Q(SCREEN_13[15:8]), .clk(pull_resistor_60_node));  // open: clr
  Register #(.trigger("high")) register_21 (
    .D(buffer_95_out), .en(decoder_19_out13), .Q(SCREEN_14[15:8]), .clk(pull_resistor_60_node));  // open: clr
  Register #(.trigger("high")) register_22 (
    .D(buffer_95_out), .en(decoder_19_out14), .Q(SCREEN_15[15:8]), .clk(pull_resistor_60_node));  // open: clr
  Register #(.trigger("high")) register_23 (
    .D(buffer_95_out), .en(decoder_19_out15), .Q(SCREEN_16[15:8]), .clk(pull_resistor_60_node));  // open: clr
  Pull_Resistor pull_resistor_78 (.node(decoder_20_out0));
  Pull_Resistor pull_resistor_79 (.node(decoder_20_out1));
  Pull_Resistor pull_resistor_80 (.node(decoder_20_out2));
  Pull_Resistor pull_resistor_81 (.node(decoder_20_out3));
  Pull_Resistor pull_resistor_82 (.node(decoder_20_out4));
  Pull_Resistor pull_resistor_83 (.node(decoder_20_out5));
  Pull_Resistor pull_resistor_84 (.node(decoder_20_out6));
  Pull_Resistor pull_resistor_85 (.node(decoder_20_out7));
  Pull_Resistor pull_resistor_86 (.node(decoder_20_out8));
  Pull_Resistor pull_resistor_87 (.node(decoder_20_out9));
  Pull_Resistor pull_resistor_88 (.node(decoder_20_out10));
  Pull_Resistor pull_resistor_89 (.node(decoder_20_out11));
  Pull_Resistor pull_resistor_90 (.node(decoder_20_out12));
  Pull_Resistor pull_resistor_91 (.node(decoder_20_out13));
  Pull_Resistor pull_resistor_92 (.node(decoder_20_out14));
  Pull_Resistor pull_resistor_93 (.node(decoder_20_out15));
  Register #(.trigger("high")) register_24 (
    .D(buffer_95_out), .en(decoder_20_out0), .Q(SCREEN_1[7:0]), .clk(pull_resistor_60_node));  // open: clr
  Register #(.trigger("high")) register_25 (
    .D(buffer_95_out), .en(decoder_20_out1), .Q(SCREEN_2[7:0]), .clk(pull_resistor_60_node));  // open: clr
  Register #(.trigger("high")) register_26 (
    .D(buffer_95_out), .en(decoder_20_out2), .Q(SCREEN_3[7:0]), .clk(pull_resistor_60_node));  // open: clr
  Register #(.trigger("high")) register_27 (
    .D(buffer_95_out), .en(decoder_20_out3), .Q(SCREEN_4[7:0]), .clk(pull_resistor_60_node));  // open: clr
  Register #(.trigger("high")) register_28 (
    .D(buffer_95_out), .en(decoder_20_out4), .Q(SCREEN_5[7:0]), .clk(pull_resistor_60_node));  // open: clr
  Register #(.trigger("high")) register_29 (
    .D(buffer_95_out), .en(decoder_20_out5), .Q(SCREEN_6[7:0]), .clk(pull_resistor_60_node));  // open: clr
  Register #(.trigger("high")) register_30 (
    .D(buffer_95_out), .en(decoder_20_out6), .Q(SCREEN_7[7:0]), .clk(pull_resistor_60_node));  // open: clr
  Register #(.trigger("high")) register_31 (
    .D(buffer_95_out), .en(decoder_20_out7), .Q(SCREEN_8[7:0]), .clk(pull_resistor_60_node));  // open: clr
  Register #(.trigger("high")) register_32 (
    .D(buffer_95_out), .en(decoder_20_out8), .Q(SCREEN_9[7:0]), .clk(pull_resistor_60_node));  // open: clr
  Register #(.trigger("high")) register_33 (
    .D(buffer_95_out), .en(decoder_20_out9), .Q(SCREEN_10[7:0]), .clk(pull_resistor_60_node));  // open: clr
  Register #(.trigger("high")) register_34 (
    .D(buffer_95_out), .en(decoder_20_out10), .Q(SCREEN_11[7:0]), .clk(pull_resistor_60_node));  // open: clr
  Register #(.trigger("high")) register_35 (
    .D(buffer_95_out), .en(decoder_20_out11), .Q(SCREEN_12[7:0]), .clk(pull_resistor_60_node));  // open: clr
  Register #(.trigger("high")) register_36 (
    .D(buffer_95_out), .en(decoder_20_out12), .Q(SCREEN_13[7:0]), .clk(pull_resistor_60_node));  // open: clr
  Register #(.trigger("high")) register_37 (
    .D(buffer_95_out), .en(decoder_20_out13), .Q(SCREEN_14[7:0]), .clk(pull_resistor_60_node));  // open: clr
  Register #(.trigger("high")) register_38 (
    .D(buffer_95_out), .en(decoder_20_out14), .Q(SCREEN_15[7:0]), .clk(pull_resistor_60_node));  // open: clr
  Register #(.trigger("high")) register_39 (
    .D(buffer_95_out), .en(decoder_20_out15), .Q(SCREEN_16[7:0]), .clk(pull_resistor_60_node));  // open: clr

  // Notes on the sheet:
  //   buffer_13 drives only 1 and floats otherwise
  //   buffer_14 drives only 1 and floats otherwise
  //   buffer_15 drives only 1 and floats otherwise
  //   buffer_16 drives only 1 and floats otherwise
  //   buffer_17 drives only 1 and floats otherwise
  //   buffer_18 drives only 1 and floats otherwise
  //   buffer_19 drives only 1 and floats otherwise
  //   buffer_20 drives only 1 and floats otherwise
  //   buffer_21 drives only 1 and floats otherwise
  //   buffer_22 drives only 1 and floats otherwise
  //   buffer_23 drives only 1 and floats otherwise
  //   buffer_24 drives only 1 and floats otherwise
  //   buffer_25 drives only 1 and floats otherwise
  //   buffer_26 drives only 1 and floats otherwise
  //   buffer_27 drives only 1 and floats otherwise
  //   0
  //   1
  //   2
  //   3
  //   4
  //   5
  //   6
  //   7
  //   8
  //   9
  //   a
  //   b
  //   c
  //   d
  //   e
  //   f
  //   buffer_32 drives only 1 and floats otherwise
  //   contents of rom_1 (hex, n*v repeats v):
  //   0 d0 0 ff b1 0 a0 1 40 c2 0 a0 20 11 0 1 a0 1 11 1 1a d0 1 8 10 4 d0 1 1 0 0 0 d2 1 0 10 4
  //   buffer_43 drives only 1 and floats otherwise
  //   buffer_44 drives only 1 and floats otherwise
  //   buffer_45 drives only 1 and floats otherwise
  //   buffer_46 drives only 1 and floats otherwise
  //   buffer_47 drives only 1 and floats otherwise
  //   buffer_48 drives only 1 and floats otherwise
  //   buffer_49 drives only 1 and floats otherwise
  //   buffer_50 drives only 1 and floats otherwise
  //   buffer_51 drives only 1 and floats otherwise
  //   buffer_52 drives only 1 and floats otherwise
  //   buffer_53 drives only 1 and floats otherwise
  //   buffer_54 drives only 1 and floats otherwise
  //   buffer_55 drives only 1 and floats otherwise
  //   buffer_56 drives only 1 and floats otherwise
  //   buffer_57 drives only 1 and floats otherwise
  //   buffer_58 drives only 1 and floats otherwise
  //   buffer_59 drives only 1 and floats otherwise
  //   buffer_60 drives only 1 and floats otherwise
  //   buffer_61 drives only 1 and floats otherwise
  //   buffer_62 drives only 1 and floats otherwise
  //   buffer_63 drives only 1 and floats otherwise
  //   buffer_64 drives only 1 and floats otherwise
  //   buffer_65 drives only 1 and floats otherwise
  //   buffer_66 drives only 1 and floats otherwise
  //   buffer_75 drives only 1 and floats otherwise
  //   buffer_76 drives only 1 and floats otherwise
  //   buffer_77 drives only 1 and floats otherwise
  //   buffer_78 drives only 1 and floats otherwise
  //   buffer_79 drives only 1 and floats otherwise
  //   buffer_80 drives only 1 and floats otherwise
  //   buffer_81 drives only 1 and floats otherwise
  //   buffer_82 drives only 1 and floats otherwise
  //   buffer_83 drives only 1 and floats otherwise
  //   buffer_84 drives only 1 and floats otherwise
  //   buffer_85 drives only 1 and floats otherwise
  //   buffer_86 drives only 1 and floats otherwise
  //   buffer_87 drives only 1 and floats otherwise
  //   buffer_88 drives only 1 and floats otherwise
  //   buffer_89 drives only 1 and floats otherwise
  //   buffer_90 drives only 1 and floats otherwise
  //   buffer_91 drives only 1 and floats otherwise
  //   buffer_92 drives only 1 and floats otherwise
  //   buffer_93 drives only 1 and floats otherwise
  //   SCRATCH PC ________________________________________________ SCRATCH PC _____________________________________________________SCRATCH PC ______________________________________________________SCRATCH PC________________________________________________________________ SCRATCH PC
endmodule
