// Logisim project PC.circ as structural Verilog: 1 circuit, main circuit main
module main (
);

  wire ADD, adder_1_cout, and_2_out, and_3_out, and_4_out, and_5_out, and_22_out, and_23_out, and_24_out,
       AtoRAM, BEQ, BtoRAM, button_1_out, button_2_out, button_3_out, CClock, CClockLoad, CFlag, ClearScreen,
       clock_1_out, Command, CtoRAM, d_ff_1_q, d_ff_2_q, d_ff_3_q, d_ff_4_q, d_ff_5_q, d_ff_6_q, d_ff_7_q,
       d_ff_8_q, d_ff_9_q, d_ff_10_q, d_ff_11_q, d_ff_12_q, d_ff_13_q, DIV, EnableKB, JMP, KBtoRAM, LogAND,
       LogNOT, LogOR, LogXOR, MODULO, MULT, not_1_out, not_2_out, not_3_out, not_4_out, not_21_out,
       not_22_out, not_23_out, not_24_out, not_25_out, not_26_out, not_27_out, not_28_out, not_29_out,
       not_30_out, not_31_out, or_1_out, or_2_out, por_1_out, por_2_out, por_3_out, pull_resistor_6_node,
       pull_resistor_9_node, pull_resistor_12_node, pull_resistor_32_node, pull_resistor_58_node,
       pull_resistor_61_node, pull_resistor_64_node, pull_resistor_67_node, pull_resistor_72_node,
       pull_resistor_75_node, pull_resistor_78_node, pull_resistor_81_node, RAMtoA, RAMtoB, RAMtoC,
       RAMtoScreen, rgb_video_1_p1, rgb_video_2_p1, RolLeft, RolRight, ROMtoA, ROMtoB, ROMtoC, SaveA, SaveB,
       SaveC, SaveCFlag, SaveIFlag, SaveNFlag, SaveNSFlag, SaveOFlag, SaveRAM, SaveScreen, SaveScreenColor,
       SaveScreenX, SaveScreenY, SetCFlag, SetIFlag, SetNFlag, SetNSFlag, SetOFlag, SetZFlag, ShiftLeft,
       ShiftRight, SUB, subtractor_1_bout;
  wire [7:0] FlagsIn, FlagsOut, rgb_video_1_p4, rgb_video_1_p5, rgb_video_2_p4, rgb_video_2_p5, ScreenX,
       ScreenY;
  wire [15:0] AIn, and_6_out, AOut, BIn, BOut, buffer_51_out, CClockAddress, CCounter, CIn, CInput,
       ColorScreen, controlled_buffer_5_out, controlled_buffer_6_out, controlled_buffer_7_out,
       controlled_buffer_8_out, controlled_buffer_9_out, controlled_buffer_10_out, controlled_buffer_11_out,
       controlled_buffer_12_out, controlled_buffer_13_out, controlled_buffer_14_out,
       controlled_buffer_15_out, controlled_buffer_16_out, controlled_buffer_17_out,
       controlled_buffer_18_out, controlled_buffer_19_out, controlled_buffer_35_out,
       controlled_buffer_36_out, controlled_buffer_37_out, controlled_buffer_38_out,
       controlled_buffer_56_out, controlled_buffer_57_out, controlled_buffer_58_out,
       controlled_buffer_59_out, controlled_buffer_62_out, controlled_buffer_63_out,
       controlled_buffer_64_out, COut, divider_1_out, divider_1_rem, divider_2_out, KBOut, multiplier_1_cout,
       multiplier_1_out, multiplier_2_out, not_5_out, or_4_out, pull_resistor_5_node, pull_resistor_8_node,
       pull_resistor_11_node, pull_resistor_20_node, pull_resistor_21_node, pull_resistor_22_node,
       pull_resistor_23_node, pull_resistor_24_node, pull_resistor_26_node, pull_resistor_30_node,
       pull_resistor_38_node, pull_resistor_39_node, pull_resistor_53_node, pull_resistor_54_node,
       pull_resistor_69_node, pull_resistor_70_node, RAMAddress, RAMIn, RAMOut, rgb_video_1_p6,
       rgb_video_2_p6, ROMOut, shifter_1_out, shifter_2_out, shifter_3_out, shifter_4_out, subtractor_1_out,
       subtractor_2_out, xor_1_out;
  wire [15:8] controlled_buffer_40_out, controlled_buffer_42_out;

  // Probe on RAMIn
  // Probe on RAMIn
  Clock clock_1 (.out(clock_1_out));
  POR #(.PorHighDuration(1), .porTransition(2)) por_1 (.out(por_1_out));
  // Probe on RAMAddress
  // Probe on RAMAddress
  RAM #(.addrWidth(16), .dataWidth(16), .enables("line")) ram_1 (
    .addr(RAMAddress), .we(SaveRAM), .clk(CClock), .din(RAMIn), .dout(RAMOut));
  Pull_Resistor pull_resistor_1 (.node(RAMAddress));
  Pull_Resistor pull_resistor_2 (.node(SaveRAM));
  Pull_Resistor pull_resistor_3 (.node(RAMIn));
  Pull_Resistor pull_resistor_4 (.node(Command));
  not not_1 (not_1_out, Command);
  Decoder #(.disabled("Z"), .select(8), .tristate("true")) decoder_1 (
    .out16(JMP), .out17(BEQ), .out64(ADD), .out65(MULT), .out66(SUB), .out67(DIV), .out68(MODULO),
    .out96(LogAND), .out97(LogOR), .out98(LogOR), .out99(LogNOT), .out100(ShiftLeft), .out101(ShiftRight),
    .out102(RolLeft), .out103(RolRight), .out160(ROMtoA), .out161(RAMtoA), .out162(AtoRAM), .out176(ROMtoB),
    .out177(RAMtoB), .out178(BtoRAM), .out192(ROMtoC), .out193(RAMtoC), .out194(CtoRAM),
    .out208(RAMtoScreen), .out209(KBtoRAM), .out210(ClearScreen), .sel(ROMOut[7:0]), .en(not_1_out));  // open: out0, out1, out2, out3, out4, out5, out6, out7, out8, out9, out10, out11, out12, out13, out14, out15, out18, out19, out20, out21, out22, out23, out24, out25, out26, out27, out28, out29, out30, out31, out32, out33, out34, out35, out36, out37, out38, out39, out40, out41, out42, out43, out44, out45, out46, out47, out48, out49, out50, out51, out52, out53, out54, out55, out56, out57, out58, out59, out60, out61, out62, out63, out69, out70, out71, out72, out73, out74, out75, out76, out77, out78, out79, out80, out81, out82, out83, out84, out85, out86, out87, out88, out89, out90, out91, out92, out93, out94, out95, out104, out105, out106, out107, out108, out109, out110, out111, out112, out113, out114, out115, out116, out117, out118, out119, out120, out121, out122, out123, out124, out125, out126, out127, out128, out129, out130, out131, out132, out133, out134, out135, out136, out137, out138, out139, out140, out141, out142, out143, out144, out145, out146, out147, out148, out149, out150, out151, out152, out153, out154, out155, out156, out157, out158, out159, out163, out164, out165, out166, out167, out168, out169, out170, out171, out172, out173, out174, out175, out179, out180, out181, out182, out183, out184, out185, out186, out187, out188, out189, out190, out191, out195, out196, out197, out198, out199, out200, out201, out202, out203, out204, out205, out206, out207, out211, out212, out213, out214, out215, out216, out217, out218, out219, out220, out221, out222, out223, out224, out225, out226, out227, out228, out229, out230, out231, out232, out233, out234, out235, out236, out237, out238, out239, out240, out241, out242, out243, out244, out245, out246, out247, out248, out249, out250, out251, out252, out253, out254, out255
  and and_1 (CClock, clock_1_out, por_1_out);
  Register #(.trigger("falling"), .width(16)) A (
    .D(pull_resistor_5_node), .en(pull_resistor_6_node), .clk(SaveA), .Q(AOut));  // open: clr
  Pull_Resistor pull_resistor_5 (.node(pull_resistor_5_node));
  assign pull_resistor_5_node = AIn;  // Buffer buffer_1, 16 bits wide
  Pull_Resistor #(.pull(1)) pull_resistor_6 (.node(pull_resistor_6_node));
  Pull_Resistor pull_resistor_7 (.node(SaveA));
  Register #(.trigger("falling"), .width(16)) B (
    .D(pull_resistor_8_node), .en(pull_resistor_9_node), .clk(SaveB), .Q(BOut));  // open: clr
  Pull_Resistor pull_resistor_8 (.node(pull_resistor_8_node));
  assign pull_resistor_8_node = BIn;  // Buffer buffer_2, 16 bits wide
  Pull_Resistor #(.pull(1)) pull_resistor_9 (.node(pull_resistor_9_node));
  Pull_Resistor pull_resistor_10 (.node(SaveB));
  Register #(.trigger("falling"), .width(16)) C (
    .D(pull_resistor_11_node), .en(pull_resistor_12_node), .clk(SaveC), .Q(COut));  // open: clr
  Pull_Resistor pull_resistor_11 (.node(pull_resistor_11_node));
  assign pull_resistor_11_node = CIn;  // Buffer buffer_3, 16 bits wide
  Pull_Resistor #(.pull(1)) pull_resistor_12 (.node(pull_resistor_12_node));
  Pull_Resistor pull_resistor_13 (.node(SaveC));
  D_Flip_Flop d_ff_1 (.D(ROMtoA), .clk(CClock), .Q(d_ff_1_q));  // open: Qn, preset, reset
  Pull_Resistor pull_resistor_14 (.node(ROMtoA));
  D_Flip_Flop d_ff_2 (.D(ROMtoB), .clk(CClock), .Q(d_ff_2_q));  // open: Qn, preset, reset
  Pull_Resistor pull_resistor_15 (.node(ROMtoB));
  D_Flip_Flop d_ff_3 (.D(ROMtoC), .clk(CClock), .Q(d_ff_3_q));  // open: Qn, preset, reset
  Pull_Resistor pull_resistor_16 (.node(ROMtoC));
  D_Flip_Flop d_ff_4 (.D(JMP), .clk(CClock), .Q(d_ff_4_q));  // open: Qn, preset, reset
  Pull_Resistor pull_resistor_17 (.node(JMP));
  buf buffer_4 (SaveCFlag, DIV);
  // Probe on AOut
  // Probe on BOut
  // Probe on COut
  buf buffer_5 (Command, d_ff_1_q);
  buf buffer_6 (SaveA, d_ff_1_q);
  assign AIn = d_ff_1_q ? ROMOut : 16'bz;  // Controlled_Buffer controlled_buffer_1
  buf buffer_7 (Command, d_ff_2_q);
  buf buffer_8 (SaveB, d_ff_2_q);
  assign BIn = d_ff_2_q ? ROMOut : 16'bz;  // Controlled_Buffer controlled_buffer_2
  buf buffer_9 (Command, d_ff_3_q);
  buf buffer_10 (SaveC, d_ff_3_q);
  assign CInput = d_ff_3_q ? ROMOut : 16'bz;  // Controlled_Buffer controlled_buffer_3
  buf buffer_11 (Command, d_ff_4_q);
  buf buffer_12 (CClockLoad, d_ff_4_q);
  assign CClockAddress = d_ff_4_q ? ROMOut : 16'bz;  // Controlled_Buffer controlled_buffer_4
  buf buffer_13 (SaveC, ADD);
  assign controlled_buffer_5_out = ADD ? AOut : 16'bz;  // Controlled_Buffer controlled_buffer_5
  Adder #(.width(16)) adder_1 (
    .a(controlled_buffer_5_out), .b(controlled_buffer_6_out), .out(CIn), .cout(adder_1_cout));  // open: cin
  assign controlled_buffer_6_out = ADD ? BOut : 16'bz;  // Controlled_Buffer controlled_buffer_6
  buf buffer_14 (SaveCFlag, ADD);
  buf buffer_15 (SaveC, SUB);
  assign controlled_buffer_7_out = SUB ? AOut : 16'bz;  // Controlled_Buffer controlled_buffer_7
  Subtractor #(.width(16)) subtractor_1 (
    .a(controlled_buffer_7_out), .b(controlled_buffer_8_out), .out(subtractor_1_out), .bout(subtractor_1_bout));  // open: bin
  assign controlled_buffer_8_out = SUB ? BOut : 16'bz;  // Controlled_Buffer controlled_buffer_8
  buf buffer_16 (SaveCFlag, SUB);
  buf buffer_17 (SaveC, MULT);
  assign controlled_buffer_9_out = MULT ? AOut : 16'bz;  // Controlled_Buffer controlled_buffer_9
  Multiplier #(.width(16)) multiplier_1 (
    .a(controlled_buffer_9_out), .b(controlled_buffer_10_out), .out(multiplier_1_out),
    .cout(multiplier_1_cout));  // open: cin
  assign controlled_buffer_10_out = MULT ? BOut : 16'bz;  // Controlled_Buffer controlled_buffer_10
  buf buffer_18 (SaveCFlag, MULT);
  buf buffer_19 (SaveC, DIV);
  assign controlled_buffer_11_out = DIV ? AOut : 16'bz;  // Controlled_Buffer controlled_buffer_11
  Divider #(.width(16)) divider_1 (
    .a(controlled_buffer_11_out), .b(controlled_buffer_12_out), .out(divider_1_out), .rem(divider_1_rem));  // open: upper
  assign controlled_buffer_12_out = DIV ? BOut : 16'bz;  // Controlled_Buffer controlled_buffer_12
  Pull_Resistor pull_resistor_18 (.node(ShiftLeft));
  assign controlled_buffer_13_out = ShiftLeft ? AOut : 16'bz;  // Controlled_Buffer controlled_buffer_13
  assign controlled_buffer_14_out = ShiftLeft ? BOut : 16'bz;  // Controlled_Buffer controlled_buffer_14
  buf buffer_20 (SaveCFlag, ShiftLeft);
  Pull_Resistor pull_resistor_19 (.node(RolLeft));
  assign controlled_buffer_15_out = RolLeft ? AOut : 16'bz;  // Controlled_Buffer controlled_buffer_15
  assign controlled_buffer_16_out = RolLeft ? BOut : 16'bz;  // Controlled_Buffer controlled_buffer_16
  buf buffer_21 (SaveCFlag, RolLeft);
  assign controlled_buffer_17_out = MODULO ? AOut : 16'bz;  // Controlled_Buffer controlled_buffer_17
  assign controlled_buffer_18_out = MODULO ? BOut : 16'bz;  // Controlled_Buffer controlled_buffer_18
  buf buffer_22 (SaveCFlag, MODULO);
  Pull_Resistor pull_resistor_20 (.node(pull_resistor_20_node));
  assign controlled_buffer_19_out = ADD ? CIn : 16'bz;  // Controlled_Buffer controlled_buffer_19
  buf buffer_23 (SetCFlag, adder_1_cout);
  Pull_Resistor pull_resistor_21 (.node(pull_resistor_21_node));
  assign CIn = SUB ? subtractor_1_out : 16'bz;  // Controlled_Buffer controlled_buffer_20
  assign SetCFlag = SUB ? subtractor_1_bout : 1'bz;  // Controlled_Buffer controlled_buffer_21
  Pull_Resistor pull_resistor_22 (.node(pull_resistor_22_node));
  assign CIn = MULT ? multiplier_1_out : 16'bz;  // Controlled_Buffer controlled_buffer_22
  Pull_Resistor pull_resistor_23 (.node(pull_resistor_23_node));
  assign CIn = DIV ? divider_1_out : 16'bz;  // Controlled_Buffer controlled_buffer_23
  buf buffer_24 (SaveC, ShiftLeft);
  assign CIn = ShiftLeft ? shifter_1_out : 16'bz;  // Controlled_Buffer controlled_buffer_24
  Shifter #(.width(16)) shifter_1 (
    .in(controlled_buffer_13_out), .\dist (controlled_buffer_14_out[3:0]), .out(shifter_1_out));
  buf buffer_25 (SaveC, RolLeft);
  Pull_Resistor pull_resistor_24 (.node(pull_resistor_24_node));
  assign CIn = RolLeft ? shifter_2_out : 16'bz;  // Controlled_Buffer controlled_buffer_25
  Shifter #(.shift("rl"), .width(16)) shifter_2 (
    .in(controlled_buffer_15_out), .\dist (controlled_buffer_16_out[3:0]), .out(shifter_2_out));
  Pull_Resistor pull_resistor_25 (.node(MODULO));
  Divider #(.width(16)) divider_2 (
    .a(controlled_buffer_17_out), .b(controlled_buffer_18_out), .out(divider_2_out));  // open: upper, rem
  Multiplier #(.width(16)) multiplier_2 (
    .a(divider_2_out), .b(controlled_buffer_18_out), .out(multiplier_2_out));  // open: cin, cout
  // Probe on RAMOut
  // Probe on RAMOut
  Comparator #(.width(16)) comparator_1 (
    .a(pull_resistor_20_node), .b(controlled_buffer_19_out), .eq(SetZFlag));  // open: gt, lt
  Comparator #(.width(16)) comparator_2 (.a(pull_resistor_21_node), .b(CIn), .eq(SetZFlag));  // open: gt, lt
  Comparator #(.width(16)) comparator_3 (.a(pull_resistor_22_node), .b(CIn), .eq(SetZFlag));  // open: gt, lt
  assign SetCFlag = MULT ? or_1_out : 1'bz;  // Controlled_Buffer controlled_buffer_26
  or or_1 (or_1_out, multiplier_1_cout[0], multiplier_1_cout[1], multiplier_1_cout[2], multiplier_1_cout[3], multiplier_1_cout[4], multiplier_1_cout[5], multiplier_1_cout[6], multiplier_1_cout[7], multiplier_1_cout[8], multiplier_1_cout[9], multiplier_1_cout[10], multiplier_1_cout[11], multiplier_1_cout[12], multiplier_1_cout[13], multiplier_1_cout[14], multiplier_1_cout[15]);
  Comparator #(.width(16)) comparator_4 (.a(pull_resistor_23_node), .b(CIn), .eq(SetZFlag));  // open: gt, lt
  assign SetCFlag = DIV ? or_2_out : 1'bz;  // Controlled_Buffer controlled_buffer_27
  or or_2 (or_2_out, divider_1_rem[0], divider_1_rem[1], divider_1_rem[2], divider_1_rem[3], divider_1_rem[4], divider_1_rem[5], divider_1_rem[6], divider_1_rem[7], divider_1_rem[8], divider_1_rem[9], divider_1_rem[10], divider_1_rem[11], divider_1_rem[12], divider_1_rem[13], divider_1_rem[14], divider_1_rem[15]);
  Pull_Resistor pull_resistor_26 (.node(pull_resistor_26_node));
  Comparator #(.width(16)) comparator_5 (.a(pull_resistor_26_node), .b(CIn), .eq(SetZFlag));  // open: gt, lt
  Comparator #(.width(16)) comparator_6 (.a(pull_resistor_24_node), .b(CIn), .eq(SetZFlag));  // open: gt, lt
  Subtractor #(.width(16)) subtractor_2 (
    .a(controlled_buffer_17_out), .b(multiplier_2_out), .out(subtractor_2_out));  // open: bin, bout
  Button button_1 (.out(button_1_out));
  ROM #(.addrWidth(16), .dataWidth(16)) rom_1 (.addr(CCounter), .data(ROMOut));
  D_Flip_Flop d_ff_5 (.D(AtoRAM), .clk(CClock), .Q(d_ff_5_q));  // open: Qn, preset, reset
  Pull_Resistor pull_resistor_27 (.node(AtoRAM));
  D_Flip_Flop d_ff_6 (.D(BtoRAM), .clk(CClock), .Q(d_ff_6_q));  // open: Qn, preset, reset
  Pull_Resistor pull_resistor_28 (.node(BtoRAM));
  D_Flip_Flop d_ff_7 (.D(CtoRAM), .clk(CClock), .Q(d_ff_7_q));  // open: Qn, preset, reset
  Pull_Resistor pull_resistor_29 (.node(CtoRAM));
  buf buffer_26 (SaveC, MODULO);
  Pull_Resistor pull_resistor_30 (.node(pull_resistor_30_node));
  Comparator #(.width(16)) comparator_7 (.a(pull_resistor_30_node), .b(CIn), .eq(SetZFlag));  // open: gt, lt
  assign CIn = MODULO ? subtractor_2_out : 16'bz;  // Controlled_Buffer controlled_buffer_28
  Counter #(.max('hffff), .width(16)) counter_1 (
    .clr(button_1_out), .load(CClockLoad), .clk(CClock), .D(CClockAddress), .Q(CCounter));  // open: up, count, carry
  Pull_Resistor pull_resistor_31 (.node(CClockLoad));
  Pull_Resistor #(.pull(1)) pull_resistor_32 (.node(pull_resistor_32_node));
  buf buffer_27 (Command, d_ff_5_q);
  buf buffer_28 (SaveRAM, d_ff_5_q);
  assign RAMIn = d_ff_5_q ? AOut : 16'bz;  // Controlled_Buffer controlled_buffer_29
  assign RAMAddress = d_ff_5_q ? ROMOut : 16'bz;  // Controlled_Buffer controlled_buffer_30
  buf buffer_29 (Command, d_ff_6_q);
  buf buffer_30 (SaveRAM, d_ff_6_q);
  assign RAMIn = d_ff_6_q ? BOut : 16'bz;  // Controlled_Buffer controlled_buffer_31
  assign RAMAddress = d_ff_6_q ? ROMOut : 16'bz;  // Controlled_Buffer controlled_buffer_32
  buf buffer_31 (Command, d_ff_7_q);
  buf buffer_32 (SaveRAM, d_ff_7_q);
  assign RAMIn = d_ff_7_q ? COut : 16'bz;  // Controlled_Buffer controlled_buffer_33
  assign RAMAddress = d_ff_7_q ? ROMOut : 16'bz;  // Controlled_Buffer controlled_buffer_34
  // Probe on FlagsOut
  Register #(.trigger("falling")) Flags (
    .D({FlagsIn[7:5], CFlag, FlagsIn[3:0]}), .en(pull_resistor_32_node), .clk(CClock), .Q(FlagsOut));  // open: clr
  Pull_Resistor pull_resistor_33 (.node(BEQ));
  Pull_Resistor pull_resistor_34 (.node(ShiftRight));
  assign controlled_buffer_35_out = ShiftRight ? AOut : 16'bz;  // Controlled_Buffer controlled_buffer_35
  assign controlled_buffer_36_out = ShiftRight ? BOut : 16'bz;  // Controlled_Buffer controlled_buffer_36
  buf buffer_33 (SaveCFlag, ShiftRight);
  Pull_Resistor pull_resistor_35 (.node(RolRight));
  assign controlled_buffer_37_out = RolRight ? AOut : 16'bz;  // Controlled_Buffer controlled_buffer_37
  Shifter #(.shift("rr"), .width(16)) shifter_3 (
    .in(controlled_buffer_37_out), .\dist (controlled_buffer_38_out[3:0]), .out(shifter_3_out));
  assign controlled_buffer_38_out = RolRight ? BOut : 16'bz;  // Controlled_Buffer controlled_buffer_38
  buf buffer_34 (SaveCFlag, RolRight);
  // Probe on ROMOut
  // Probe on ROMOut
  Pull_Resistor pull_resistor_36 (.node(RAMtoScreen));
  buf buffer_35 (SaveScreenX, RAMtoScreen);
  assign RAMAddress = RAMtoScreen ? 16'h7ffd : 16'bz;  // Controlled_Buffer controlled_buffer_39
  assign {controlled_buffer_40_out, ScreenX} = RAMtoScreen ? RAMOut : 16'bz;  // Controlled_Buffer controlled_buffer_40
  D_Flip_Flop d_ff_8 (.D(RAMtoScreen), .clk(CClock), .Q(d_ff_8_q));  // open: Qn, preset, reset
  assign RAMAddress = d_ff_8_q ? 16'h7ffe : 16'bz;  // Controlled_Buffer controlled_buffer_41
  assign {controlled_buffer_42_out, ScreenY} = d_ff_8_q ? RAMOut : 16'bz;  // Controlled_Buffer controlled_buffer_42
  D_Flip_Flop d_ff_9 (.D(d_ff_8_q), .clk(CClock), .Q(d_ff_9_q));  // open: Qn, preset, reset
  assign RAMAddress = d_ff_9_q ? 16'h7fff : 16'bz;  // Controlled_Buffer controlled_buffer_43
  assign ColorScreen = d_ff_9_q ? RAMOut : 16'bz;  // Controlled_Buffer controlled_buffer_44
  Pull_Resistor pull_resistor_37 (.node(KBtoRAM));
  buf buffer_36 (SaveRAM, KBtoRAM);
  buf buffer_37 (EnableKB, KBtoRAM);
  assign RAMAddress = KBtoRAM ? 16'h7000 : 16'bz;  // Controlled_Buffer controlled_buffer_45
  assign RAMIn = KBtoRAM ? KBOut : 16'bz;  // Controlled_Buffer controlled_buffer_46
  D_Flip_Flop d_ff_10 (.D(BEQ), .clk(CClock), .Q(d_ff_10_q));  // open: Qn, preset, reset
  buf buffer_38 (SaveC, ShiftRight);
  Pull_Resistor pull_resistor_38 (.node(pull_resistor_38_node));
  assign CIn = ShiftRight ? shifter_4_out : 16'bz;  // Controlled_Buffer controlled_buffer_47
  Shifter #(.shift("lr"), .width(16)) shifter_4 (
    .in(controlled_buffer_35_out), .\dist (controlled_buffer_36_out[3:0]), .out(shifter_4_out));
  buf buffer_39 (SaveC, RolRight);
  Pull_Resistor pull_resistor_39 (.node(pull_resistor_39_node));
  assign CIn = RolRight ? shifter_3_out : 16'bz;  // Controlled_Buffer controlled_buffer_48
  Keyboard #(.buflen(255)) keyboard_1 (.clk(CClock), .re(EnableKB), .data(KBOut[6:0]));  // open: clr, avail
  Pull_Resistor pull_resistor_40 (.node(EnableKB));
  D_Flip_Flop d_ff_11 (.D(RAMtoA), .clk(CClock), .Q(d_ff_11_q));  // open: Qn, preset, reset
  Pull_Resistor pull_resistor_41 (.node(RAMtoA));
  assign AIn = d_ff_11_q ? RAMOut : 16'bz;  // Controlled_Buffer controlled_buffer_49
  assign RAMAddress = d_ff_11_q ? ROMOut : 16'bz;  // Controlled_Buffer controlled_buffer_50
  D_Flip_Flop d_ff_12 (.D(RAMtoB), .clk(CClock), .Q(d_ff_12_q));  // open: Qn, preset, reset
  Pull_Resistor pull_resistor_42 (.node(RAMtoB));
  assign BIn = d_ff_12_q ? RAMOut : 16'bz;  // Controlled_Buffer controlled_buffer_51
  assign RAMAddress = d_ff_12_q ? ROMOut : 16'bz;  // Controlled_Buffer controlled_buffer_52
  D_Flip_Flop d_ff_13 (.D(RAMtoC), .clk(CClock), .Q(d_ff_13_q));  // open: Qn, preset, reset
  Pull_Resistor pull_resistor_43 (.node(RAMtoC));
  assign CIn = d_ff_13_q ? RAMOut : 16'bz;  // Controlled_Buffer controlled_buffer_53
  assign RAMAddress = d_ff_13_q ? ROMOut : 16'bz;  // Controlled_Buffer controlled_buffer_54
  buf buffer_40 (SaveScreenY, d_ff_8_q);
  buf buffer_41 (SaveScreenColor, d_ff_9_q);
  buf buffer_42 (SaveScreen, d_ff_9_q);
  buf buffer_43 (Command, d_ff_10_q);
  and and_2 (and_2_out, d_ff_10_q, FlagsIn[3]);
  buf buffer_44 (CClockLoad, and_2_out);
  assign CClockAddress = and_2_out ? ROMOut : 16'bz;  // Controlled_Buffer controlled_buffer_55
  Comparator #(.width(16)) comparator_8 (.a(pull_resistor_38_node), .b(CIn), .eq(SetZFlag));  // open: gt, lt
  Comparator #(.width(16)) comparator_9 (.a(pull_resistor_39_node), .b(CIn), .eq(SetZFlag));  // open: gt, lt
  buf buffer_45 (Command, d_ff_11_q);
  buf buffer_46 (SaveA, d_ff_11_q);
  buf buffer_47 (Command, d_ff_12_q);
  buf buffer_48 (SaveB, d_ff_12_q);
  buf buffer_49 (Command, d_ff_13_q);
  buf buffer_50 (SaveC, d_ff_13_q);
  assign buffer_51_out = KBOut;  // Buffer buffer_51, 16 bits wide
  Pull_Resistor pull_resistor_44 (.node(buffer_51_out));
  // Probe on buffer_51_out
  // Probe on buffer_51_out
  Button button_2 (.out(button_2_out));
  POR #(.PorHighDuration(1)) por_2 (.out(por_2_out));
  Pull_Resistor pull_resistor_45 (.node(ClearScreen));
  Pull_Resistor pull_resistor_46 (.node(SaveScreenX));
  not not_2 (not_2_out, CClock);
  not not_3 (not_3_out, CClock);
  // RGB_Video #(.cursor("No Cursor"), .height(256), .width(256)) rgb_video_1: pin names not known; wires that end beside it: rgb_video_1_p1, CClock, SaveScreen, rgb_video_1_p4, rgb_video_1_p5, rgb_video_1_p6
  or or_3 (rgb_video_1_p1, por_2_out, button_2_out, ClearScreen);
  Register u_ScreenX (.D(ScreenX), .clk(and_3_out), .Q(rgb_video_1_p4));  // open: en, clr
  and and_3 (and_3_out, SaveScreenX, not_2_out);
  Register u_ScreenY (.D(ScreenY), .clk(and_4_out), .Q(rgb_video_1_p5));  // open: en, clr
  Pull_Resistor pull_resistor_47 (.node(SaveScreenY));
  and and_4 (and_4_out, SaveScreenY, not_3_out);
  Pull_Resistor pull_resistor_48 (.node(rgb_video_1_p6));
  Pull_Resistor pull_resistor_49 (.node(SaveScreen));
  assign controlled_buffer_56_out = LogOR ? AOut : 16'bz;  // Controlled_Buffer controlled_buffer_56
  assign controlled_buffer_57_out = LogOR ? BOut : 16'bz;  // Controlled_Buffer controlled_buffer_57
  assign controlled_buffer_58_out = LogAND ? AOut : 16'bz;  // Controlled_Buffer controlled_buffer_58
  assign controlled_buffer_59_out = LogAND ? BOut : 16'bz;  // Controlled_Buffer controlled_buffer_59
  Pull_Resistor pull_resistor_50 (.node(SaveScreenColor));
  and and_5 (and_5_out, SaveScreenColor, not_4_out);
  not not_4 (not_4_out, CClock);
  Pull_Resistor pull_resistor_51 (.node(LogOR));
  or or_4 (or_4_out[0], controlled_buffer_56_out[0], controlled_buffer_57_out[0]);
  or or_5 (or_4_out[1], controlled_buffer_56_out[1], controlled_buffer_57_out[1]);
  or or_6 (or_4_out[2], controlled_buffer_56_out[2], controlled_buffer_57_out[2]);
  or or_7 (or_4_out[3], controlled_buffer_56_out[3], controlled_buffer_57_out[3]);
  or or_8 (or_4_out[4], controlled_buffer_56_out[4], controlled_buffer_57_out[4]);
  or or_9 (or_4_out[5], controlled_buffer_56_out[5], controlled_buffer_57_out[5]);
  or or_10 (or_4_out[6], controlled_buffer_56_out[6], controlled_buffer_57_out[6]);
  or or_11 (or_4_out[7], controlled_buffer_56_out[7], controlled_buffer_57_out[7]);
  or or_12 (or_4_out[8], controlled_buffer_56_out[8], controlled_buffer_57_out[8]);
  or or_13 (or_4_out[9], controlled_buffer_56_out[9], controlled_buffer_57_out[9]);
  or or_14 (or_4_out[10], controlled_buffer_56_out[10], controlled_buffer_57_out[10]);
  or or_15 (or_4_out[11], controlled_buffer_56_out[11], controlled_buffer_57_out[11]);
  or or_16 (or_4_out[12], controlled_buffer_56_out[12], controlled_buffer_57_out[12]);
  or or_17 (or_4_out[13], controlled_buffer_56_out[13], controlled_buffer_57_out[13]);
  or or_18 (or_4_out[14], controlled_buffer_56_out[14], controlled_buffer_57_out[14]);
  or or_19 (or_4_out[15], controlled_buffer_56_out[15], controlled_buffer_57_out[15]);
  Pull_Resistor pull_resistor_52 (.node(LogAND));
  and and_6 (and_6_out[0], controlled_buffer_58_out[0], controlled_buffer_59_out[0]);
  and and_7 (and_6_out[1], controlled_buffer_58_out[1], controlled_buffer_59_out[1]);
  and and_8 (and_6_out[2], controlled_buffer_58_out[2], controlled_buffer_59_out[2]);
  and and_9 (and_6_out[3], controlled_buffer_58_out[3], controlled_buffer_59_out[3]);
  and and_10 (and_6_out[4], controlled_buffer_58_out[4], controlled_buffer_59_out[4]);
  and and_11 (and_6_out[5], controlled_buffer_58_out[5], controlled_buffer_59_out[5]);
  and and_12 (and_6_out[6], controlled_buffer_58_out[6], controlled_buffer_59_out[6]);
  and and_13 (and_6_out[7], controlled_buffer_58_out[7], controlled_buffer_59_out[7]);
  and and_14 (and_6_out[8], controlled_buffer_58_out[8], controlled_buffer_59_out[8]);
  and and_15 (and_6_out[9], controlled_buffer_58_out[9], controlled_buffer_59_out[9]);
  and and_16 (and_6_out[10], controlled_buffer_58_out[10], controlled_buffer_59_out[10]);
  and and_17 (and_6_out[11], controlled_buffer_58_out[11], controlled_buffer_59_out[11]);
  and and_18 (and_6_out[12], controlled_buffer_58_out[12], controlled_buffer_59_out[12]);
  and and_19 (and_6_out[13], controlled_buffer_58_out[13], controlled_buffer_59_out[13]);
  and and_20 (and_6_out[14], controlled_buffer_58_out[14], controlled_buffer_59_out[14]);
  and and_21 (and_6_out[15], controlled_buffer_58_out[15], controlled_buffer_59_out[15]);
  Register #(.trigger("high"), .width(16)) ScreenColor (
    .D(ColorScreen), .clk(and_5_out), .Q(rgb_video_1_p6));  // open: en, clr
  buf buffer_52 (SaveC, LogOR);
  buf buffer_53 (SaveCFlag, LogOR);
  assign CIn = LogOR ? or_4_out : 16'bz;  // Controlled_Buffer controlled_buffer_60
  buf buffer_54 (SaveC, LogAND);
  buf buffer_55 (SaveCFlag, LogAND);
  assign CIn = LogAND ? and_6_out : 16'bz;  // Controlled_Buffer controlled_buffer_61
  Pull_Resistor pull_resistor_53 (.node(pull_resistor_53_node));
  Comparator #(.width(16)) comparator_10 (.a(pull_resistor_53_node), .b(CIn), .eq(SetZFlag));  // open: gt, lt
  Pull_Resistor pull_resistor_54 (.node(pull_resistor_54_node));
  Comparator #(.width(16)) comparator_11 (.a(pull_resistor_54_node), .b(CIn), .eq(SetZFlag));  // open: gt, lt
  assign controlled_buffer_62_out = LogXOR ? AOut : 16'bz;  // Controlled_Buffer controlled_buffer_62
  assign controlled_buffer_63_out = LogXOR ? BOut : 16'bz;  // Controlled_Buffer controlled_buffer_63
  assign controlled_buffer_64_out = LogNOT ? AOut : 16'bz;  // Controlled_Buffer controlled_buffer_64
  Pull_Resistor pull_resistor_55 (.node(LogXOR));
  xor xor_1 (xor_1_out[0], controlled_buffer_62_out[0], controlled_buffer_63_out[0]);
  xor xor_2 (xor_1_out[1], controlled_buffer_62_out[1], controlled_buffer_63_out[1]);
  xor xor_3 (xor_1_out[2], controlled_buffer_62_out[2], controlled_buffer_63_out[2]);
  xor xor_4 (xor_1_out[3], controlled_buffer_62_out[3], controlled_buffer_63_out[3]);
  xor xor_5 (xor_1_out[4], controlled_buffer_62_out[4], controlled_buffer_63_out[4]);
  xor xor_6 (xor_1_out[5], controlled_buffer_62_out[5], controlled_buffer_63_out[5]);
  xor xor_7 (xor_1_out[6], controlled_buffer_62_out[6], controlled_buffer_63_out[6]);
  xor xor_8 (xor_1_out[7], controlled_buffer_62_out[7], controlled_buffer_63_out[7]);
  xor xor_9 (xor_1_out[8], controlled_buffer_62_out[8], controlled_buffer_63_out[8]);
  xor xor_10 (xor_1_out[9], controlled_buffer_62_out[9], controlled_buffer_63_out[9]);
  xor xor_11 (xor_1_out[10], controlled_buffer_62_out[10], controlled_buffer_63_out[10]);
  xor xor_12 (xor_1_out[11], controlled_buffer_62_out[11], controlled_buffer_63_out[11]);
  xor xor_13 (xor_1_out[12], controlled_buffer_62_out[12], controlled_buffer_63_out[12]);
  xor xor_14 (xor_1_out[13], controlled_buffer_62_out[13], controlled_buffer_63_out[13]);
  xor xor_15 (xor_1_out[14], controlled_buffer_62_out[14], controlled_buffer_63_out[14]);
  xor xor_16 (xor_1_out[15], controlled_buffer_62_out[15], controlled_buffer_63_out[15]);
  Pull_Resistor pull_resistor_56 (.node(LogNOT));
  not not_5 (not_5_out[0], controlled_buffer_64_out[0]);
  not not_6 (not_5_out[1], controlled_buffer_64_out[1]);
  not not_7 (not_5_out[2], controlled_buffer_64_out[2]);
  not not_8 (not_5_out[3], controlled_buffer_64_out[3]);
  not not_9 (not_5_out[4], controlled_buffer_64_out[4]);
  not not_10 (not_5_out[5], controlled_buffer_64_out[5]);
  not not_11 (not_5_out[6], controlled_buffer_64_out[6]);
  not not_12 (not_5_out[7], controlled_buffer_64_out[7]);
  not not_13 (not_5_out[8], controlled_buffer_64_out[8]);
  not not_14 (not_5_out[9], controlled_buffer_64_out[9]);
  not not_15 (not_5_out[10], controlled_buffer_64_out[10]);
  not not_16 (not_5_out[11], controlled_buffer_64_out[11]);
  not not_17 (not_5_out[12], controlled_buffer_64_out[12]);
  not not_18 (not_5_out[13], controlled_buffer_64_out[13]);
  not not_19 (not_5_out[14], controlled_buffer_64_out[14]);
  not not_20 (not_5_out[15], controlled_buffer_64_out[15]);
  Pull_Resistor pull_resistor_57 (.node(SetNFlag));
  Pull_Resistor pull_resistor_58 (.node(pull_resistor_58_node));
  assign pull_resistor_58_node = not_21_out ? FlagsOut[0] : 1'bz;  // Controlled_Buffer controlled_buffer_65
  not not_21 (not_21_out, SaveNFlag);
  Pull_Resistor pull_resistor_59 (.node(SaveNFlag));
  Pull_Resistor pull_resistor_60 (.node(SetIFlag));
  Pull_Resistor pull_resistor_61 (.node(pull_resistor_61_node));
  assign pull_resistor_61_node = not_22_out ? FlagsOut[2] : 1'bz;  // Controlled_Buffer controlled_buffer_66
  not not_22 (not_22_out, SaveIFlag);
  Pull_Resistor pull_resistor_62 (.node(SaveIFlag));
  Pull_Resistor pull_resistor_63 (.node(SetCFlag));
  Pull_Resistor pull_resistor_64 (.node(pull_resistor_64_node));
  assign pull_resistor_64_node = not_23_out ? FlagsOut[4] : 1'bz;  // Controlled_Buffer controlled_buffer_67
  not not_23 (not_23_out, SaveCFlag);
  Pull_Resistor pull_resistor_65 (.node(SaveCFlag));
  Pull_Resistor pull_resistor_66 (.node(SetNSFlag));
  Pull_Resistor pull_resistor_67 (.node(pull_resistor_67_node));
  assign pull_resistor_67_node = not_24_out ? FlagsOut[6] : 1'bz;  // Controlled_Buffer controlled_buffer_68
  not not_24 (not_24_out, SaveNSFlag);
  Pull_Resistor pull_resistor_68 (.node(SaveNSFlag));
  buf buffer_56 (SaveC, LogXOR);
  buf buffer_57 (SaveCFlag, LogXOR);
  assign CIn = LogXOR ? xor_1_out : 16'bz;  // Controlled_Buffer controlled_buffer_69
  buf buffer_58 (SaveC, LogNOT);
  buf buffer_59 (SaveCFlag, LogNOT);
  assign CIn = LogNOT ? not_5_out : 16'bz;  // Controlled_Buffer controlled_buffer_70
  or or_20 (FlagsIn[0], SetNFlag, pull_resistor_58_node);
  Register #(.trigger("falling"), .width(1)) D0N (.D(FlagsIn[0]), .clk(CClock));  // open: en, Q, clr
  or or_21 (FlagsIn[2], SetIFlag, pull_resistor_61_node);
  Register #(.trigger("falling"), .width(1)) D2I (.D(FlagsIn[2]), .clk(CClock));  // open: en, Q, clr
  or or_22 (CFlag, SetCFlag, pull_resistor_64_node);
  Register #(.trigger("falling"), .width(1)) D4C (.D(CFlag), .clk(CClock));  // open: en, Q, clr
  or or_23 (FlagsIn[6], SetNSFlag, pull_resistor_67_node);
  Register #(.trigger("falling"), .width(1)) D6 (.D(FlagsIn[6]), .clk(CClock));  // open: en, Q, clr
  Pull_Resistor pull_resistor_69 (.node(pull_resistor_69_node));
  Pull_Resistor pull_resistor_70 (.node(pull_resistor_70_node));
  Comparator #(.width(16)) comparator_12 (.a(pull_resistor_70_node), .b(CIn), .eq(SetZFlag));  // open: gt, lt
  Comparator #(.width(16)) comparator_13 (.a(pull_resistor_69_node), .b(CIn), .eq(SetZFlag));  // open: gt, lt
  Pull_Resistor pull_resistor_71 (.node(SetOFlag));
  Pull_Resistor pull_resistor_72 (.node(pull_resistor_72_node));
  assign pull_resistor_72_node = not_25_out ? FlagsOut[1] : 1'bz;  // Controlled_Buffer controlled_buffer_71
  not not_25 (not_25_out, SaveOFlag);
  Pull_Resistor pull_resistor_73 (.node(SaveOFlag));
  Pull_Resistor pull_resistor_74 (.node(SetZFlag));
  Pull_Resistor pull_resistor_75 (.node(pull_resistor_75_node));
  assign pull_resistor_75_node = not_26_out ? FlagsOut[3] : 1'bz;  // Controlled_Buffer controlled_buffer_72
  not not_26 (not_26_out, SaveCFlag);
  Pull_Resistor pull_resistor_76 (.node(SaveCFlag));
  Pull_Resistor pull_resistor_77 (.node(SetNSFlag));
  Pull_Resistor pull_resistor_78 (.node(pull_resistor_78_node));
  assign pull_resistor_78_node = not_27_out ? FlagsOut[5] : 1'bz;  // Controlled_Buffer controlled_buffer_73
  not not_27 (not_27_out, SaveNSFlag);
  Pull_Resistor pull_resistor_79 (.node(SaveNSFlag));
  Pull_Resistor pull_resistor_80 (.node(SetNSFlag));
  Pull_Resistor pull_resistor_81 (.node(pull_resistor_81_node));
  assign pull_resistor_81_node = not_28_out ? FlagsOut[7] : 1'bz;  // Controlled_Buffer controlled_buffer_74
  not not_28 (not_28_out, SaveNSFlag);
  Pull_Resistor pull_resistor_82 (.node(SaveNSFlag));
  or or_24 (FlagsIn[1], SetOFlag, pull_resistor_72_node);
  Register #(.trigger("falling"), .width(1)) D1O (.D(FlagsIn[1]), .clk(CClock));  // open: en, Q, clr
  or or_25 (FlagsIn[3], SetZFlag, pull_resistor_75_node);
  Register #(.trigger("falling"), .width(1)) D3Z (.D(FlagsIn[3]), .clk(CClock));  // open: en, Q, clr
  or or_26 (FlagsIn[5], SetNSFlag, pull_resistor_78_node);
  Register #(.trigger("falling"), .width(1)) D5 (.D(FlagsIn[5]), .clk(CClock));  // open: en, Q, clr
  or or_27 (FlagsIn[7], SetNSFlag, pull_resistor_81_node);
  Register #(.trigger("falling"), .width(1)) D7 (.D(FlagsIn[7]), .clk(CClock));  // open: en, Q, clr
  Pull_Resistor pull_resistor_83 (.node({FlagsIn[7:5], CFlag, FlagsIn[3:0]}));
  Button button_3 (.out(button_3_out));
  POR #(.PorHighDuration(1)) por_3 (.out(por_3_out));
  Pull_Resistor pull_resistor_84 (.node(ClearScreen));
  Pull_Resistor pull_resistor_85 (.node(SaveScreenX));
  not not_29 (not_29_out, CClock);
  Pull_Resistor pull_resistor_86 (.node(SaveScreenY));
  not not_30 (not_30_out, CClock);
  // RGB_Video #(.cursor("No Cursor"), .height(256), .scale(8), .width(256)) rgb_video_2: pin names not known; wires that end beside it: rgb_video_2_p1, CClock, SaveScreen, rgb_video_2_p4, rgb_video_2_p5, rgb_video_2_p6
  or or_28 (rgb_video_2_p1, por_3_out, button_3_out, ClearScreen);
  Pull_Resistor pull_resistor_87 (.node(SaveScreen));
  Register register_1 (.D(ScreenX), .clk(and_22_out), .Q(rgb_video_2_p4));  // open: en, clr
  and and_22 (and_22_out, SaveScreenX, not_29_out);
  Register register_2 (.D(ScreenY), .clk(and_23_out), .Q(rgb_video_2_p5));  // open: en, clr
  and and_23 (and_23_out, SaveScreenY, not_30_out);
  Pull_Resistor pull_resistor_88 (.node(rgb_video_2_p6));
  Register #(.trigger("high"), .width(16)) register_3 (
    .D(ColorScreen), .clk(and_24_out), .Q(rgb_video_2_p6));  // open: en, clr
  Pull_Resistor pull_resistor_89 (.node(SaveScreenColor));
  and and_24 (and_24_out, SaveScreenColor, not_31_out);
  not not_31 (not_31_out, CClock);

  // Other names for the same wires on the sheet: NFlag = FlagsIn[0]; OFlag = FlagsIn[1]; IFlag = FlagsIn[2];
  //   ZFlag = FlagsIn[3]; FlagsIn[4] = CFlag; SaveZFlag = SaveCFlag

  // Notes on the sheet:
  //   buffer_5 drives only 1 and floats otherwise
  //   buffer_6 drives only 1 and floats otherwise
  //   buffer_7 drives only 1 and floats otherwise
  //   buffer_8 drives only 1 and floats otherwise
  //   buffer_9 drives only 1 and floats otherwise
  //   buffer_10 drives only 1 and floats otherwise
  //   buffer_11 drives only 1 and floats otherwise
  //   buffer_12 drives only 1 and floats otherwise
  //   buffer_20 drives only 1 and floats otherwise
  //   buffer_21 drives only 1 and floats otherwise
  //   buffer_22 drives only 1 and floats otherwise
  //   buffer_24 drives only 1 and floats otherwise
  //   buffer_25 drives only 1 and floats otherwise
  //   Negative
  //   Overflow
  //   Interrupt Disable
  //   Zero
  //   Carry
  //   contents of rom_1 (hex, n*v repeats v):
  //   a0 f000 a2 7fff a0 ffff a2 7ffd a0 aa55 a2 2000 a1 7ffd b0 1 40 c2 7ffd a1 7ffd b0 8 65 c2 7ffe a1
  //   7ffd b0 10 44 c2 0 a0 1 b1 0 64 0 c2 1 a1 2000 b1 1 60 0 c2 2 a1 2 b0 ffff 41 c2 7fff d0 0 0 0 10 c
  //   buffer_26 drives only 1 and floats otherwise
  //   buffer_27 drives only 1 and floats otherwise
  //   buffer_28 drives only 1 and floats otherwise
  //   buffer_29 drives only 1 and floats otherwise
  //   buffer_30 drives only 1 and floats otherwise
  //   buffer_31 drives only 1 and floats otherwise
  //   buffer_32 drives only 1 and floats otherwise
  //   buffer_33 drives only 1 and floats otherwise
  //   buffer_34 drives only 1 and floats otherwise
  //   buffer_35 drives only 1 and floats otherwise
  //   buffer_36 drives only 1 and floats otherwise
  //   buffer_37 drives only 1 and floats otherwise
  //   buffer_38 drives only 1 and floats otherwise
  //   buffer_39 drives only 1 and floats otherwise
  //   buffer_40 drives only 1 and floats otherwise
  //   buffer_41 drives only 1 and floats otherwise
  //   buffer_42 drives only 1 and floats otherwise
  //   buffer_43 drives only 1 and floats otherwise
  //   buffer_44 drives only 1 and floats otherwise
  //   buffer_45 drives only 1 and floats otherwise
  //   buffer_46 drives only 1 and floats otherwise
  //   buffer_47 drives only 1 and floats otherwise
  //   buffer_48 drives only 1 and floats otherwise
  //   buffer_49 drives only 1 and floats otherwise
  //   buffer_50 drives only 1 and floats otherwise
  //   buffer_52 drives only 1 and floats otherwise
  //   buffer_53 drives only 1 and floats otherwise
  //   buffer_54 drives only 1 and floats otherwise
  //   buffer_55 drives only 1 and floats otherwise
  //   Negative
  //   Overflow
  //   Interrupt Disable
  //   Zero
  //   Carry
  //   buffer_56 drives only 1 and floats otherwise
  //   buffer_57 drives only 1 and floats otherwise
  //   buffer_58 drives only 1 and floats otherwise
  //   buffer_59 drives only 1 and floats otherwise
endmodule
