// Logisim project PC.circ as structural Verilog: 1 circuit, main circuit main
module main (
);

  wire ADD, adder_1_cout, and_2_out, and_3_out, and_4_out, and_5_out, AtoRAM, BEQ, BtoRAM, button_1_out,
       CClock, CClockLoad, CFlag, clock_1_out, Command, CtoRAM, d_ff_1_q, d_ff_2_q, d_ff_3_q, d_ff_4_q,
       d_ff_5_q, d_ff_6_q, d_ff_7_q, d_ff_8_q, d_ff_9_q, d_ff_10_q, d_ff_11_q, d_ff_12_q, d_ff_13_q, JMP,
       MULT, not_1_out, not_2_out, not_3_out, not_4_out, not_5_out, not_6_out, not_7_out, not_8_out,
       not_9_out, not_10_out, not_11_out, not_12_out, or_1_out, or_4_out, or_7_out, or_8_out, por_1_out,
       por_2_out, pull_resistor_32_node, pull_resistor_35_node, pull_resistor_38_node, pull_resistor_41_node,
       pull_resistor_44_node, pull_resistor_47_node, pull_resistor_50_node, pull_resistor_53_node, RAMtoA,
       RAMtoB, RAMtoC, RAMtoScreen, ROMtoA, ROMtoB, ROMtoC, SaveA, SaveB, SaveC, SaveCFlag, SaveIFlag,
       SaveNFlag, SaveNSFlag, SaveOFlag, SaveRAM, SaveScreen, SaveScreenColor, SaveScreenX, SaveScreenY,
       SetCFlag, SetIFlag, SetNFlag, SetNSFlag, SetOFlag, SetZFlag, SUB, subtractor_1_bout;
  wire [7:0] FlagsIn, FlagsOut, rgb_video_1_p4, rgb_video_1_p5, ScreenX, ScreenY;
  wire [15:0] AIn, AOut, BIn, BOut, CClockAddress, CCounter, CIn, CInput, ColorScreen,
       controlled_buffer_5_out, controlled_buffer_6_out, controlled_buffer_7_out, controlled_buffer_8_out,
       controlled_buffer_9_out, controlled_buffer_13_out, controlled_buffer_14_out, COut,
       pull_resistor_5_node, pull_resistor_7_node, pull_resistor_9_node, pull_resistor_16_node,
       pull_resistor_17_node, RAMAddress, RAMIn, RAMOut, rgb_video_1_p6, ROMOut, subtractor_1_out;
  wire [15:8] controlled_buffer_22_out, controlled_buffer_24_out;

  // Probe on RAMIn
  // Probe on RAMIn
  Clock clock_1 (.out(clock_1_out));
  POR #(.PorHighDuration(1), .porTransition(2)) por_1 (.out(por_1_out));
  // Probe on RAMAddress
  // Probe on RAMAddress
  RAM #(.addrWidth(16), .dataWidth(16), .enables("line")) ram_1 (
    .addr(RAMAddress), .we(SaveRAM), .clk(CClock), .din(RAMIn), .dout(RAMOut));
  Pull_Resistor pull_resistor_1 (.node(RAMAddress));
  Pull_Resistor pull_resistor_2 (.node(SaveRAM));
  Pull_Resistor pull_resistor_3 (.node(RAMIn));
  Pull_Resistor pull_resistor_4 (.node(Command));
  not not_1 (not_1_out, Command);
  Decoder #(.disabled("Z"), .select(8), .tristate("true")) decoder_1 (
    .out16(JMP), .out17(BEQ), .out64(ADD), .out65(MULT), .out66(SUB), .out160(ROMtoA), .out161(RAMtoA),
    .out162(AtoRAM), .out176(ROMtoB), .out177(RAMtoB), .out178(BtoRAM), .out192(ROMtoC), .out193(RAMtoC),
    .out194(CtoRAM), .out208(RAMtoScreen), .sel(ROMOut[7:0]), .en(not_1_out));  // open: out0, out1, out2, out3, out4, out5, out6, out7, out8, out9, out10, out11, out12, out13, out14, out15, out18, out19, out20, out21, out22, out23, out24, out25, out26, out27, out28, out29, out30, out31, out32, out33, out34, out35, out36, out37, out38, out39, out40, out41, out42, out43, out44, out45, out46, out47, out48, out49, out50, out51, out52, out53, out54, out55, out56, out57, out58, out59, out60, out61, out62, out63, out67, out68, out69, out70, out71, out72, out73, out74, out75, out76, out77, out78, out79, out80, out81, out82, out83, out84, out85, out86, out87, out88, out89, out90, out91, out92, out93, out94, out95, out96, out97, out98, out99, out100, out101, out102, out103, out104, out105, out106, out107, out108, out109, out110, out111, out112, out113, out114, out115, out116, out117, out118, out119, out120, out121, out122, out123, out124, out125, out126, out127, out128, out129, out130, out131, out132, out133, out134, out135, out136, out137, out138, out139, out140, out141, out142, out143, out144, out145, out146, out147, out148, out149, out150, out151, out152, out153, out154, out155, out156, out157, out158, out159, out163, out164, out165, out166, out167, out168, out169, out170, out171, out172, out173, out174, out175, out179, out180, out181, out182, out183, out184, out185, out186, out187, out188, out189, out190, out191, out195, out196, out197, out198, out199, out200, out201, out202, out203, out204, out205, out206, out207, out209, out210, out211, out212, out213, out214, out215, out216, out217, out218, out219, out220, out221, out222, out223, out224, out225, out226, out227, out228, out229, out230, out231, out232, out233, out234, out235, out236, out237, out238, out239, out240, out241, out242, out243, out244, out245, out246, out247, out248, out249, out250, out251, out252, out253, out254, out255
  and and_1 (CClock, clock_1_out, por_1_out);
  Register #(.trigger("falling"), .width(16)) A (.D(pull_resistor_5_node), .clk(SaveA), .Q(AOut));  // open: en, clr
  Pull_Resistor pull_resistor_5 (.node(pull_resistor_5_node));
  assign pull_resistor_5_node = AIn;  // Buffer buffer_1, 16 bits wide
  Pull_Resistor pull_resistor_6 (.node(SaveA));
  Register #(.trigger("falling"), .width(16)) B (.D(pull_resistor_7_node), .clk(SaveB), .Q(BOut));  // open: en, clr
  Pull_Resistor pull_resistor_7 (.node(pull_resistor_7_node));
  assign pull_resistor_7_node = BIn;  // Buffer buffer_2, 16 bits wide
  Pull_Resistor pull_resistor_8 (.node(SaveB));
  Register #(.trigger("falling"), .width(16)) C (.D(pull_resistor_9_node), .clk(SaveC), .Q(COut));  // open: en, clr
  Pull_Resistor pull_resistor_9 (.node(pull_resistor_9_node));
  assign pull_resistor_9_node = CIn;  // Buffer buffer_3, 16 bits wide
  Pull_Resistor pull_resistor_10 (.node(SaveC));
  D_Flip_Flop d_ff_1 (.D(ROMtoA), .clk(CClock), .Q(d_ff_1_q));  // open: Qn, preset, reset
  Pull_Resistor pull_resistor_11 (.node(ROMtoA));
  D_Flip_Flop d_ff_2 (.D(ROMtoB), .clk(CClock), .Q(d_ff_2_q));  // open: Qn, preset, reset
  Pull_Resistor pull_resistor_12 (.node(ROMtoB));
  D_Flip_Flop d_ff_3 (.D(ROMtoC), .clk(CClock), .Q(d_ff_3_q));  // open: Qn, preset, reset
  Pull_Resistor pull_resistor_13 (.node(ROMtoC));
  D_Flip_Flop d_ff_4 (.D(JMP), .clk(CClock), .Q(d_ff_4_q));  // open: Qn, preset, reset
  Pull_Resistor pull_resistor_14 (.node(JMP));
  buf buffer_4 (Command, d_ff_1_q);
  buf buffer_5 (SaveA, d_ff_1_q);
  assign AIn = d_ff_1_q ? ROMOut : 16'bz;  // Controlled_Buffer controlled_buffer_1
  buf buffer_6 (Command, d_ff_2_q);
  buf buffer_7 (SaveB, d_ff_2_q);
  assign BIn = d_ff_2_q ? ROMOut : 16'bz;  // Controlled_Buffer controlled_buffer_2
  buf buffer_8 (Command, d_ff_3_q);
  buf buffer_9 (SaveC, d_ff_3_q);
  assign CInput = d_ff_3_q ? ROMOut : 16'bz;  // Controlled_Buffer controlled_buffer_3
  buf buffer_10 (Command, d_ff_4_q);
  buf buffer_11 (CClockLoad, d_ff_4_q);
  assign CClockAddress = d_ff_4_q ? ROMOut : 16'bz;  // Controlled_Buffer controlled_buffer_4
  buf buffer_12 (SaveC, ADD);
  assign controlled_buffer_5_out = ADD ? AOut : 16'bz;  // Controlled_Buffer controlled_buffer_5
  Adder #(.width(16)) adder_1 (
    .a(controlled_buffer_5_out), .b(controlled_buffer_6_out), .out(CIn), .cout(adder_1_cout));  // open: cin
  assign controlled_buffer_6_out = ADD ? BOut : 16'bz;  // Controlled_Buffer controlled_buffer_6
  buf buffer_13 (SaveCFlag, ADD);
  buf buffer_14 (SaveC, SUB);
  assign controlled_buffer_7_out = SUB ? AOut : 16'bz;  // Controlled_Buffer controlled_buffer_7
  Subtractor #(.width(16)) subtractor_1 (
    .a(controlled_buffer_7_out), .b(controlled_buffer_8_out), .out(subtractor_1_out), .bout(subtractor_1_bout));  // open: bin
  assign controlled_buffer_8_out = SUB ? BOut : 16'bz;  // Controlled_Buffer controlled_buffer_8
  buf buffer_15 (SaveCFlag, SUB);
  D_Flip_Flop d_ff_5 (.D(BEQ), .clk(CClock), .Q(d_ff_5_q));  // open: Qn, preset, reset
  Pull_Resistor pull_resistor_15 (.node(BEQ));
  Register #(.trigger("falling")) Flags (
    .D({FlagsIn[7:5], CFlag, FlagsIn[3:0]}), .clk(CClock), .Q(FlagsOut));  // open: en, clr
  Pull_Resistor pull_resistor_16 (.node(pull_resistor_16_node));
  assign controlled_buffer_9_out = SaveCFlag ? CIn : 16'bz;  // Controlled_Buffer controlled_buffer_9
  buf buffer_16 (SetCFlag, adder_1_cout);
  Pull_Resistor pull_resistor_17 (.node(pull_resistor_17_node));
  assign CIn = SUB ? subtractor_1_out : 16'bz;  // Controlled_Buffer controlled_buffer_10
  assign SetCFlag = SUB ? subtractor_1_bout : 1'bz;  // Controlled_Buffer controlled_buffer_11
  buf buffer_17 (Command, d_ff_5_q);
  and and_2 (and_2_out, d_ff_5_q, FlagsIn[3]);
  buf buffer_18 (CClockLoad, and_2_out);
  assign CClockAddress = and_2_out ? ROMOut : 16'bz;  // Controlled_Buffer controlled_buffer_12
  // Probe on FlagsOut
  // Probe on RAMOut
  // Probe on RAMOut
  Comparator #(.width(16)) comparator_1 (
    .a(pull_resistor_16_node), .b(controlled_buffer_9_out), .eq(SetZFlag));  // open: gt, lt
  Comparator #(.width(16)) comparator_2 (.a(pull_resistor_17_node), .b(CIn), .eq(SetZFlag));  // open: gt, lt
  Button button_1 (.out(button_1_out));
  ROM #(.addrWidth(16), .dataWidth(16)) rom_1 (.addr(CCounter), .data(ROMOut));
  D_Flip_Flop d_ff_6 (.D(AtoRAM), .clk(CClock), .Q(d_ff_6_q));  // open: Qn, preset, reset
  Pull_Resistor pull_resistor_18 (.node(AtoRAM));
  D_Flip_Flop d_ff_7 (.D(BtoRAM), .clk(CClock), .Q(d_ff_7_q));  // open: Qn, preset, reset
  Pull_Resistor pull_resistor_19 (.node(BtoRAM));
  D_Flip_Flop d_ff_8 (.D(CtoRAM), .clk(CClock), .Q(d_ff_8_q));  // open: Qn, preset, reset
  Pull_Resistor pull_resistor_20 (.node(CtoRAM));
  buf buffer_19 (SaveC, MULT);
  assign controlled_buffer_13_out = MULT ? AOut : 16'bz;  // Controlled_Buffer controlled_buffer_13
  assign controlled_buffer_14_out = MULT ? BOut : 16'bz;  // Controlled_Buffer controlled_buffer_14
  Counter #(.max('hffff), .width(16)) counter_1 (
    .clr(button_1_out), .load(CClockLoad), .clk(CClock), .D(CClockAddress), .Q(CCounter));  // open: up, count, carry
  Pull_Resistor pull_resistor_21 (.node(CClockLoad));
  buf buffer_20 (Command, d_ff_6_q);
  buf buffer_21 (SaveRAM, d_ff_6_q);
  assign RAMIn = d_ff_6_q ? AOut : 16'bz;  // Controlled_Buffer controlled_buffer_15
  assign RAMAddress = d_ff_6_q ? ROMOut : 16'bz;  // Controlled_Buffer controlled_buffer_16
  buf buffer_22 (Command, d_ff_7_q);
  buf buffer_23 (SaveRAM, d_ff_7_q);
  assign RAMIn = d_ff_7_q ? BOut : 16'bz;  // Controlled_Buffer controlled_buffer_17
  assign RAMAddress = d_ff_7_q ? ROMOut : 16'bz;  // Controlled_Buffer controlled_buffer_18
  buf buffer_24 (Command, d_ff_8_q);
  buf buffer_25 (SaveRAM, d_ff_8_q);
  assign RAMIn = d_ff_8_q ? COut : 16'bz;  // Controlled_Buffer controlled_buffer_19
  assign RAMAddress = d_ff_8_q ? ROMOut : 16'bz;  // Controlled_Buffer controlled_buffer_20
  Multiplier #(.width(16)) multiplier_1 (
    .a(controlled_buffer_13_out), .b(controlled_buffer_14_out), .out(CIn));  // open: cin, cout
  // Probe on ROMOut
  // Probe on ROMOut
  Pull_Resistor pull_resistor_22 (.node(RAMtoScreen));
  buf buffer_26 (SaveScreenX, RAMtoScreen);
  assign RAMAddress = RAMtoScreen ? 16'h7ffd : 16'bz;  // Controlled_Buffer controlled_buffer_21
  assign {controlled_buffer_22_out, ScreenX} = RAMtoScreen ? RAMOut : 16'bz;  // Controlled_Buffer controlled_buffer_22
  D_Flip_Flop d_ff_9 (.D(RAMtoScreen), .clk(CClock), .Q(d_ff_9_q));  // open: Qn, preset, reset
  assign RAMAddress = d_ff_9_q ? 16'h7ffe : 16'bz;  // Controlled_Buffer controlled_buffer_23
  assign {controlled_buffer_24_out, ScreenY} = d_ff_9_q ? RAMOut : 16'bz;  // Controlled_Buffer controlled_buffer_24
  D_Flip_Flop d_ff_10 (.D(d_ff_9_q), .clk(CClock), .Q(d_ff_10_q));  // open: Qn, preset, reset
  assign RAMAddress = d_ff_10_q ? 16'h7fff : 16'bz;  // Controlled_Buffer controlled_buffer_25
  assign ColorScreen = d_ff_10_q ? RAMOut : 16'bz;  // Controlled_Buffer controlled_buffer_26
  D_Flip_Flop d_ff_11 (.D(RAMtoA), .clk(CClock), .Q(d_ff_11_q));  // open: Qn, preset, reset
  Pull_Resistor pull_resistor_23 (.node(RAMtoA));
  assign AIn = d_ff_11_q ? RAMOut : 16'bz;  // Controlled_Buffer controlled_buffer_27
  assign RAMAddress = d_ff_11_q ? ROMOut : 16'bz;  // Controlled_Buffer controlled_buffer_28
  D_Flip_Flop d_ff_12 (.D(RAMtoB), .clk(CClock), .Q(d_ff_12_q));  // open: Qn, preset, reset
  Pull_Resistor pull_resistor_24 (.node(RAMtoB));
  assign BIn = d_ff_12_q ? RAMOut : 16'bz;  // Controlled_Buffer controlled_buffer_29
  assign RAMAddress = d_ff_12_q ? ROMOut : 16'bz;  // Controlled_Buffer controlled_buffer_30
  D_Flip_Flop d_ff_13 (.D(RAMtoC), .clk(CClock), .Q(d_ff_13_q));  // open: Qn, preset, reset
  Pull_Resistor pull_resistor_25 (.node(RAMtoC));
  assign CIn = d_ff_13_q ? RAMOut : 16'bz;  // Controlled_Buffer controlled_buffer_31
  assign RAMAddress = d_ff_13_q ? ROMOut : 16'bz;  // Controlled_Buffer controlled_buffer_32
  buf buffer_27 (SaveScreenY, d_ff_9_q);
  buf buffer_28 (SaveScreenColor, d_ff_10_q);
  buf buffer_29 (SaveScreen, d_ff_10_q);
  buf buffer_30 (Command, d_ff_11_q);
  buf buffer_31 (SaveA, d_ff_11_q);
  buf buffer_32 (Command, d_ff_12_q);
  buf buffer_33 (SaveB, d_ff_12_q);
  buf buffer_34 (Command, d_ff_13_q);
  buf buffer_35 (SaveC, d_ff_13_q);
  Pull_Resistor pull_resistor_26 (.node(SaveScreenX));
  not not_2 (not_2_out, CClock);
  not not_3 (not_3_out, CClock);
  POR #(.PorHighDuration(1)) por_2 (.out(por_2_out));
  // RGB_Video #(.height(256), .width(256)) rgb_video_1: pin names not known; wires that end beside it: por_2_out, CClock, SaveScreen, rgb_video_1_p4, rgb_video_1_p5, rgb_video_1_p6
  Register u_ScreenX (.D(ScreenX), .clk(and_3_out), .Q(rgb_video_1_p4));  // open: en, clr
  and and_3 (and_3_out, SaveScreenX, not_2_out);
  Register u_ScreenY (.D(ScreenY), .clk(and_4_out), .Q(rgb_video_1_p5));  // open: en, clr
  Pull_Resistor pull_resistor_27 (.node(SaveScreenY));
  and and_4 (and_4_out, SaveScreenY, not_3_out);
  Pull_Resistor pull_resistor_28 (.node(rgb_video_1_p6));
  Pull_Resistor pull_resistor_29 (.node(SaveScreen));
  Pull_Resistor pull_resistor_30 (.node(SaveScreenColor));
  and and_5 (and_5_out, SaveScreenColor, not_4_out);
  not not_4 (not_4_out, CClock);
  Register #(.trigger("high"), .width(16)) ScreenColor (
    .D(ColorScreen), .clk(and_5_out), .Q(rgb_video_1_p6));  // open: en, clr
  Pull_Resistor pull_resistor_31 (.node(SetNFlag));
  Pull_Resistor pull_resistor_32 (.node(pull_resistor_32_node));
  assign pull_resistor_32_node = not_5_out ? FlagsOut[0] : 1'bz;  // Controlled_Buffer controlled_buffer_33
  not not_5 (not_5_out, SaveNFlag);
  Pull_Resistor pull_resistor_33 (.node(SaveNFlag));
  Pull_Resistor pull_resistor_34 (.node(SetIFlag));
  Pull_Resistor pull_resistor_35 (.node(pull_resistor_35_node));
  assign pull_resistor_35_node = not_6_out ? FlagsOut[2] : 1'bz;  // Controlled_Buffer controlled_buffer_34
  not not_6 (not_6_out, SaveIFlag);
  Pull_Resistor pull_resistor_36 (.node(SaveIFlag));
  Pull_Resistor pull_resistor_37 (.node(SetCFlag));
  Pull_Resistor pull_resistor_38 (.node(pull_resistor_38_node));
  assign pull_resistor_38_node = not_7_out ? FlagsOut[4] : 1'bz;  // Controlled_Buffer controlled_buffer_35
  not not_7 (not_7_out, SaveCFlag);
  Pull_Resistor pull_resistor_39 (.node(SaveCFlag));
  Pull_Resistor pull_resistor_40 (.node(SetNSFlag));
  Pull_Resistor pull_resistor_41 (.node(pull_resistor_41_node));
  assign pull_resistor_41_node = not_8_out ? FlagsOut[6] : 1'bz;  // Controlled_Buffer controlled_buffer_36
  not not_8 (not_8_out, SaveNSFlag);
  Pull_Resistor pull_resistor_42 (.node(SaveNSFlag));
  Register #(.trigger("falling"), .width(1)) DN (.D(or_1_out), .clk(CClock), .Q(FlagsIn[0]));  // open: en, clr
  or or_1 (or_1_out, SetNFlag, pull_resistor_32_node);
  or or_2 (FlagsIn[2], SetIFlag, pull_resistor_35_node);
  Register #(.trigger("falling"), .width(1)) DI (.D(FlagsIn[2]), .clk(CClock));  // open: en, Q, clr
  or or_3 (CFlag, SetCFlag, pull_resistor_38_node);
  Register #(.trigger("falling"), .width(1)) DC (.D(CFlag), .clk(CClock));  // open: en, Q, clr
  Register #(.trigger("falling"), .width(1)) register_1 (.D(or_4_out), .clk(CClock), .Q(FlagsIn[6]));  // open: en, clr
  or or_4 (or_4_out, SetNSFlag, pull_resistor_41_node);
  Pull_Resistor pull_resistor_43 (.node(SetOFlag));
  Pull_Resistor pull_resistor_44 (.node(pull_resistor_44_node));
  assign pull_resistor_44_node = not_9_out ? FlagsOut[1] : 1'bz;  // Controlled_Buffer controlled_buffer_37
  not not_9 (not_9_out, SaveOFlag);
  Pull_Resistor pull_resistor_45 (.node(SaveOFlag));
  Pull_Resistor pull_resistor_46 (.node(SetZFlag));
  Pull_Resistor pull_resistor_47 (.node(pull_resistor_47_node));
  assign pull_resistor_47_node = not_10_out ? FlagsOut[3] : 1'bz;  // Controlled_Buffer controlled_buffer_38
  not not_10 (not_10_out, SaveCFlag);
  Pull_Resistor pull_resistor_48 (.node(SaveCFlag));
  Pull_Resistor pull_resistor_49 (.node(SetNSFlag));
  Pull_Resistor pull_resistor_50 (.node(pull_resistor_50_node));
  assign pull_resistor_50_node = not_11_out ? FlagsOut[5] : 1'bz;  // Controlled_Buffer controlled_buffer_39
  not not_11 (not_11_out, SaveNSFlag);
  Pull_Resistor pull_resistor_51 (.node(SaveNSFlag));
  Pull_Resistor pull_resistor_52 (.node(SetNSFlag));
  Pull_Resistor pull_resistor_53 (.node(pull_resistor_53_node));
  assign pull_resistor_53_node = not_12_out ? FlagsOut[7] : 1'bz;  // Controlled_Buffer controlled_buffer_40
  not not_12 (not_12_out, SaveNSFlag);
  Pull_Resistor pull_resistor_54 (.node(SaveNSFlag));
  or or_5 (FlagsIn[1], SetOFlag, pull_resistor_44_node);
  Register #(.trigger("falling"), .width(1)) DO (.D(FlagsIn[1]), .clk(CClock));  // open: en, Q, clr
  or or_6 (FlagsIn[3], SetZFlag, pull_resistor_47_node);
  Register #(.trigger("falling"), .width(1)) DZ (.D(FlagsIn[3]), .clk(CClock));  // open: en, Q, clr
  Register #(.trigger("falling"), .width(1)) register_2 (.D(or_7_out), .clk(CClock), .Q(FlagsIn[5]));  // open: en, clr
  or or_7 (or_7_out, SetNSFlag, pull_resistor_50_node);
  Register #(.trigger("falling"), .width(1)) register_3 (.D(or_8_out), .clk(CClock), .Q(FlagsIn[7]));  // open: en, clr
  or or_8 (or_8_out, SetNSFlag, pull_resistor_53_node);
  Pull_Resistor pull_resistor_55 (.node({FlagsIn[7:5], CFlag, FlagsIn[3:0]}));

  // Other names for the same wires on the sheet: NFlag = FlagsIn[0]; OFlag = FlagsIn[1]; IFlag = FlagsIn[2];
  //   ZFlag = FlagsIn[3]; FlagsIn[4] = CFlag; SaveZFlag = SaveCFlag

  // Notes on the sheet:
  //   buffer_4 drives only 1 and floats otherwise
  //   buffer_5 drives only 1 and floats otherwise
  //   buffer_6 drives only 1 and floats otherwise
  //   buffer_7 drives only 1 and floats otherwise
  //   buffer_8 drives only 1 and floats otherwise
  //   buffer_9 drives only 1 and floats otherwise
  //   buffer_10 drives only 1 and floats otherwise
  //   buffer_11 drives only 1 and floats otherwise
  //   buffer_17 drives only 1 and floats otherwise
  //   buffer_18 drives only 1 and floats otherwise
  //   Negative
  //   Overflow
  //   Interrupt Disable
  //   Zero
  //   Carry
  //   contents of rom_1 (hex, n*v repeats v):
  //   a0 ffff a2 7fff a0 100 a2 7000 a2 7ffe 10 1000 500*0 a0 3583*0 a2 7000 b0 1 42 c2 7ffd a1 7ffd d0 0
  //   0 0 11 1011 10 1004 a1 7ffe 42 c2 7ffe a1 7000 a2 7000 10 1004 d0 0 0 0 10 1000 14*0 10 1000 190*0
  //   10
  //   buffer_20 drives only 1 and floats otherwise
  //   buffer_21 drives only 1 and floats otherwise
  //   buffer_22 drives only 1 and floats otherwise
  //   buffer_23 drives only 1 and floats otherwise
  //   buffer_24 drives only 1 and floats otherwise
  //   buffer_25 drives only 1 and floats otherwise
  //   buffer_26 drives only 1 and floats otherwise
  //   buffer_27 drives only 1 and floats otherwise
  //   buffer_28 drives only 1 and floats otherwise
  //   buffer_29 drives only 1 and floats otherwise
  //   buffer_30 drives only 1 and floats otherwise
  //   buffer_31 drives only 1 and floats otherwise
  //   buffer_32 drives only 1 and floats otherwise
  //   buffer_33 drives only 1 and floats otherwise
  //   buffer_34 drives only 1 and floats otherwise
  //   buffer_35 drives only 1 and floats otherwise
  //   Negative
  //   Overflow
  //   Interrupt Disable
  //   Zero
  //   Carry
endmodule
